// Logisim project alu2.circ as structural Verilog: 4 circuits, main circuit main
module main (
  input  [15:0] in_1,
  input  [15:0] in_2,
  input  [3:0] in_3,
  input  in_4,
  input  reg_write,
  input  b_src,
  input  [1:0] reg_sel,
  input  [1:0] a_src,
  input  [3:0] in_9,
  input  pc_src,
  input  ir_write,
  input  PC_write,
  input  mem_write,
  input  ir_fetch,
  input  op_fetch
);

  wire alu_1_c_out, alu_1_n, alu_1_v, alu_1_z, clock_1_out, not_1_out, not_2_out, not_3_out, not_4_out,
       or_1_out;
  wire [15:0] alu_1_result, alu_2_result, bit_extender_1_out, bit_extender_2_out, IR_q, multiplexer_1_out,
       multiplexer_2_out, multiplexer_3_out, OP_q, PC_q, ram_1_data, reg_1_out, reg_latch_q;

  Clock clock_1 (.out(clock_1_out));
  not not_1 (not_1_out, 1'b1);
  assign bit_extender_1_out = {{15{1'b0}}, not_1_out};  // Bit_Extender bit_extender_1
  assign bit_extender_2_out = {{15{1'b0}}, 1'b1};  // Bit_Extender bit_extender_2
  Multiplexer #(.width(16)) multiplexer_1 (.in0(alu_2_result), .out(multiplexer_1_out), .sel(not_2_out));  // open: in1
  not not_2 (not_2_out, or_1_out);
  Register #(.width(16)) PC (.D(multiplexer_1_out), .en(or_1_out), .Q(PC_q), .clk(clock_1_out));  // open: clr
  Multiplexer #(.width(16)) multiplexer_2 (
    .in0(bit_extender_1_out), .in1(bit_extender_2_out), .out(multiplexer_2_out), .sel(or_1_out));
  Multiplexer #(.select(2), .width(16)) multiplexer_3 (
    .in0(PC_q), .out(multiplexer_3_out), .sel(a_src));  // open: in1, in2, in3
  or or_1 (or_1_out, ir_fetch, op_fetch);
  alu alu_1 (
    .V(alu_1_v), .N(alu_1_n), .result(alu_1_result), .C_out(alu_1_c_out), .Z(alu_1_z), .A(in_1), .B(in_2),
    .C_in(in_4), .op(in_3));
  // Probe on alu_1_result
  alu alu_2 (
    .result(alu_2_result), .A(multiplexer_3_out), .B(multiplexer_2_out), .op(in_9));  // open: V, N, C_out, Z, C_in
  not not_3 (not_3_out, mem_write);
  RAM #(.addrWidth(16), .dataWidth(16), .bus("separate")) ram_1 (
    .addr(PC_q), .data(ram_1_data), .str(mem_write), .clk(clock_1_out), .ld(not_3_out));  // open: din, sel, clr
  // Probe on ram_1_data
  Register #(.width(16)) IR (.D(ram_1_data), .en(ir_fetch), .Q(IR_q), .clk(clock_1_out));  // open: clr
  \reg  reg_1 (.clock(clock_1_out), .in(reg_latch_q), .in_3(reg_sel), .write(reg_write), .out(reg_1_out));
  Register #(.width(16)) OP (.D(ram_1_data), .en(op_fetch), .Q(OP_q), .clk(clock_1_out));  // open: clr
  not not_4 (not_4_out, clock_1_out);
  Register #(.width(16)) reg_latch (.D(reg_1_out), .Q(reg_latch_q), .clk(not_4_out));  // open: en, clr
  // Probe on reg_1_out
  // Probe on reg_latch_q
endmodule

module oveflow (
  input  a,
  input  b,
  input  r,
  output v
);

  wire and_1_out, and_2_out, and_3_out, and_4_out, not_1_out, not_2_out, not_3_out;

  not not_1 (not_1_out, a);
  not not_2 (not_2_out, b);
  and and_1 (and_1_out, not_1_out, not_2_out);
  and and_2 (and_2_out, a, b);
  not not_3 (not_3_out, r);
  and and_3 (and_3_out, and_1_out, r);
  and and_4 (and_4_out, and_2_out, not_3_out);
  or or_1 (v, and_3_out, and_4_out);
endmodule

module alu (
  input  C_in,
  input  [15:0] A,
  input  [15:0] B,
  input  [3:0] op,
  output V,
  output N,
  output [15:0] result,
  output C_out,
  output Z
);

  wire adder_1_cout, subtractor_1_bout;
  wire [15:0] adder_1_out, and_1_out, divider_1_out, multiplier_1_out, negator_1_out, not_1_out, or_1_out,
       subtractor_1_out, xor_1_out;

  Multiplier #(.width(16)) multiplier_1 (.a(A), .b(B), .out(multiplier_1_out));  // open: cin, cout
  Adder #(.width(16)) adder_1 (.a(A), .b(B), .out(adder_1_out), .cin(C_in), .cout(adder_1_cout));
  Divider #(.width(16)) divider_1 (.a(A), .b(B), .out(divider_1_out));  // open: upper, rem
  assign and_1_out = A & B;  // AND_Gate and_1, 16 bits wide
  assign or_1_out = A | B;  // OR_Gate or_1, 16 bits wide
  assign xor_1_out = A ^ B;  // XOR_Gate xor_1, 16 bits wide
  Subtractor #(.width(16)) subtractor_1 (.a(A), .b(B), .out(subtractor_1_out), .bin(C_in), .bout(subtractor_1_bout));
  assign not_1_out = ~A;  // NOT_Gate not_1, 16 bits wide
  Negator #(.width(16)) negator_1 (.in(A), .out(negator_1_out));
  Comparator #(.width(16)) comparator_1 (.a(A), .b(B));  // open: gt, eq, lt
  Multiplexer #(.select(4), .width(16)) multiplexer_1 (
    .in0(adder_1_out), .in1(subtractor_1_out), .in2(multiplier_1_out), .in3(divider_1_out), .in4(and_1_out),
    .in5(or_1_out), .in6(not_1_out), .in7(xor_1_out), .in13(negator_1_out), .out({N, result[14:0]}), .sel(op));  // open: in8, in9, in10, in11, in12, in14, in15
  Multiplexer #(.select(4)) multiplexer_2 (
    .in0(adder_1_cout), .in1(subtractor_1_bout), .out(C_out), .sel(op));  // open: in2, in3, in4, in5, in6, in7, in8, in9, in10, in11, in12, in13, in14, in15
  oveflow oveflow_1 (.a(A[15]), .b(B[15]), .r(N), .v(V));
  Pull_Resistor pull_resistor_1 (.node(C_out));
  nor nor_1 (Z, result[0], result[1], result[2], result[3], result[4], result[5], result[6], result[7], result[8], result[9], result[10], result[11], result[12], result[13], result[14], N);

  assign result[15] = N;
endmodule

module \reg  (
  input  clock,
  input  [15:0] in,
  input  [1:0] in_3,
  input  write,
  output [15:0] out
);

  wire demultiplexer_1_out0, demultiplexer_1_out1, demultiplexer_1_out2, demultiplexer_1_out3;
  wire [15:0] A_q, B_q, X_q, Y_q;

  Register #(.width(16)) A (.D(in), .en(demultiplexer_1_out0), .Q(A_q), .clk(clock));  // open: clr
  Register #(.width(16)) X (.D(in), .en(demultiplexer_1_out2), .Q(X_q), .clk(clock));  // open: clr
  Demultiplexer #(.select(2)) demultiplexer_1 (
    .out0(demultiplexer_1_out0), .out1(demultiplexer_1_out1), .out2(demultiplexer_1_out2),
    .out3(demultiplexer_1_out3), .in(write), .sel(in_3));
  Register #(.width(16)) B (.D(in), .en(demultiplexer_1_out1), .Q(B_q), .clk(clock));  // open: clr
  Register #(.width(16)) Y (.D(in), .en(demultiplexer_1_out3), .Q(Y_q), .clk(clock));  // open: clr
  Multiplexer #(.select(2), .width(16)) multiplexer_1 (
    .in0(A_q), .in1(B_q), .in2(X_q), .in3(Y_q), .out(out), .sel(in_3));
endmodule
