// Logisim project arm.circ as structural Verilog
module main (
  input  [7:0] in_1,
  input  [7:0] in_2,
  input  in_3,
  input  [7:0] in_4,
  input  [7:0] in_5,
  input  in_6,
  input  [31:0] in_7,
  input  [4:0] in_8,
  output [7:0] out_9,
  output [7:0] out_10,
  output [7:0] out_11,
  output [7:0] out_12,
  output [7:0] out_13,
  output out_14,
  output ZERO,
  output SIGN,
  output [7:0] RESULT,
  output CARRY,
  output OVERFLOW,
  output [7:0] out_20,
  output out_21,
  output [31:0] out_22
);

  wire adder_2_cout;
  wire [7:0] multiplexer_1_out, negator_1_out;
  wire [9:9] shifter_1_out;

  Negator negator_1 (.in(in_5), .out(negator_1_out));
  Multiplexer #(.width(8), .enable("false")) multiplexer_1 (
    .in0(in_5), .in1(negator_1_out), .out(multiplexer_1_out), .sel(in_6));
  Shifter #(.width(10), .shift("rr")) shifter_1 (
    .in({in_3, in_4, 1'b0}), .\dist (4'b0001), .out({shifter_1_out[9], out_20, out_21}));
  Adder adder_1 (.a(in_4), .b(multiplexer_1_out), .out(RESULT), .cin(in_3), .cout(CARRY));
  Shifter #(.width(32), .shift("rr")) shifter_2 (.in(in_7), .\dist (in_8), .out(out_22));
  Divider divider_1 (.a(in_4), .b(in_5), .out(out_9), .upper(in_1), .rem(out_10));
  Multiplier multiplier_1 (.a(in_4), .b(in_5), .out(out_11), .cin(in_2), .cout(out_12));
  Subtractor subtractor_1 (.a(in_4), .b(in_5), .out(out_13), .bout(out_14));  // open: bin
  Adder #(.width(7)) adder_2 (.a(in_4[6:0]), .b(multiplexer_1_out[6:0]), .cin(in_3), .cout(adder_2_cout));  // open: out
  xor xor_1 (OVERFLOW, CARRY, adder_2_cout);
  Comparator comparator_1 (.a(RESULT), .b({8{1'b0}}), .eq(ZERO));  // open: gt, lt

  assign SIGN = RESULT[7];
endmodule

module prefetch (
  input  in_1,
  input  PC_WRT,
  output [15:0] out_3
);

  wire and_1_out, and_2_out, clock_1_out, counter_1_q, decoder_1_out0, decoder_1_out1, decoder_2_out0,
       decoder_2_out1, not_1_out;
  wire [15:0] adder_1_out, IR0_q, IR1_q, PC_q, ram_1_data;

  Clock clock_1 (.out(clock_1_out));
  Counter #(.width(1), .max('h1)) counter_1 (
    .count(in_1), .Q(counter_1_q), .clk(clock_1_out));  // open: load, D, carry, clr
  Decoder #(.enable("false")) decoder_1 (.out0(decoder_1_out0), .out1(decoder_1_out1), .sel(counter_1_q));
  and and_1 (and_1_out, in_1, decoder_1_out1);
  Adder #(.width(16)) adder_1 (.a(PC_q), .b(16'h1), .out(adder_1_out));  // open: cin, cout
  and and_2 (and_2_out, in_1, decoder_1_out0);
  Register #(.width(16)) PC (.D(adder_1_out), .en(PC_WRT), .Q(PC_q), .clk(clock_1_out));  // open: clr
  Register #(.width(16)) IR0 (.D(ram_1_data), .en(and_2_out), .Q(IR0_q), .clk(clock_1_out));  // open: clr
  Register #(.width(16)) IR1 (.D(ram_1_data), .en(and_1_out), .Q(IR1_q), .clk(clock_1_out));  // open: clr
  not not_1 (not_1_out, counter_1_q);
  Decoder #(.enable("false")) decoder_2 (.out0(decoder_2_out0), .out1(decoder_2_out1), .sel(not_1_out));
  Multiplexer #(.width(16), .enable("false")) multiplexer_1 (.in0(IR0_q), .in1(IR1_q), .out(out_3), .sel(not_1_out));
  RAM #(.addrWidth(16), .dataWidth(16)) ram_1 (
    .addr(PC_q), .data(ram_1_data), .clk(clock_1_out));  // open: sel, ld, clr
endmodule

// REGISTER
module \reg  (
  input  [3:0] SRC1_REG,
  input  [3:0] SRC2_REG,
  input  R0_ZERO,
  input  CLOCK,
  input  WRITE,
  input  [31:0] DATA_IN,
  input  [3:0] DST_REG,
  output [31:0] SRC1_OUT,
  output [31:0] SRC2_OUT
);

  wire and_1_out, and_2_out, and_3_out, and_4_out, and_5_out, and_6_out, and_7_out, and_8_out, and_9_out,
       and_10_out, and_11_out, and_12_out, and_13_out, and_14_out, and_15_out, and_16_out, decoder_1_out0,
       decoder_1_out1, decoder_1_out2, decoder_1_out3, decoder_1_out4, decoder_1_out5, decoder_1_out6,
       decoder_1_out7, decoder_1_out8, decoder_1_out9, decoder_1_out10, decoder_1_out11, decoder_1_out12,
       decoder_1_out13, decoder_1_out14, decoder_1_out15, decoder_2_out0, decoder_2_out1, decoder_2_out2,
       decoder_2_out3, decoder_2_out4, decoder_2_out5, decoder_2_out6, decoder_2_out7, decoder_2_out8,
       decoder_2_out9, decoder_2_out10, decoder_2_out11, decoder_2_out12, decoder_2_out13, decoder_2_out14,
       decoder_2_out15, decoder_3_out0, decoder_3_out1, decoder_3_out2, decoder_3_out3, decoder_3_out4,
       decoder_3_out5, decoder_3_out6, decoder_3_out7, decoder_3_out8, decoder_3_out9, decoder_3_out10,
       decoder_3_out11, decoder_3_out12, decoder_3_out13, decoder_3_out14, decoder_3_out15;
  wire [31:0] multiplexer_1_out, R0_q, R1_q, R2_q, R3_q, R4_q, R5_q, R6_q, R7_q, R8_q, R9_q, R10_q, R11_q,
       R12_q, R13_q, R14_q, R15_q;

  Decoder #(.select(4), .enable("false")) decoder_1 (
    .out0(decoder_1_out0), .out1(decoder_1_out1), .out2(decoder_1_out2), .out3(decoder_1_out3),
    .out4(decoder_1_out4), .out5(decoder_1_out5), .out6(decoder_1_out6), .out7(decoder_1_out7),
    .out8(decoder_1_out8), .out9(decoder_1_out9), .out10(decoder_1_out10), .out11(decoder_1_out11),
    .out12(decoder_1_out12), .out13(decoder_1_out13), .out14(decoder_1_out14), .out15(decoder_1_out15),
    .sel(DST_REG));
  and and_1 (and_1_out, decoder_1_out0, WRITE);
  and and_2 (and_2_out, decoder_1_out1, WRITE);
  and and_3 (and_3_out, decoder_1_out2, WRITE);
  and and_4 (and_4_out, decoder_1_out3, WRITE);
  and and_5 (and_5_out, decoder_1_out4, WRITE);
  and and_6 (and_6_out, decoder_1_out5, WRITE);
  and and_7 (and_7_out, decoder_1_out6, WRITE);
  and and_8 (and_8_out, decoder_1_out7, WRITE);
  and and_9 (and_9_out, decoder_1_out8, WRITE);
  and and_10 (and_10_out, decoder_1_out9, WRITE);
  and and_11 (and_11_out, decoder_1_out10, WRITE);
  and and_12 (and_12_out, decoder_1_out11, WRITE);
  and and_13 (and_13_out, decoder_1_out12, WRITE);
  and and_14 (and_14_out, decoder_1_out13, WRITE);
  and and_15 (and_15_out, decoder_1_out14, WRITE);
  and and_16 (and_16_out, decoder_1_out15, WRITE);
  Multiplexer #(.width(32), .enable("false")) multiplexer_1 (
    .in0(R0_q), .in1({32{1'b0}}), .out(multiplexer_1_out), .sel(R0_ZERO));
  Register #(.width(32)) R0 (.D(DATA_IN), .en(and_1_out), .Q(R0_q), .clk(CLOCK));  // open: clr
  Register #(.width(32)) R1 (.D(DATA_IN), .en(and_2_out), .Q(R1_q), .clk(CLOCK));  // open: clr
  Register #(.width(32)) R2 (.D(DATA_IN), .en(and_3_out), .Q(R2_q), .clk(CLOCK));  // open: clr
  Register #(.width(32)) R3 (.D(DATA_IN), .en(and_4_out), .Q(R3_q), .clk(CLOCK));  // open: clr
  Register #(.width(32)) R4 (.D(DATA_IN), .en(and_5_out), .Q(R4_q), .clk(CLOCK));  // open: clr
  Register #(.width(32)) R5 (.D(DATA_IN), .en(and_6_out), .Q(R5_q), .clk(CLOCK));  // open: clr
  Register #(.width(32)) R6 (.D(DATA_IN), .en(and_7_out), .Q(R6_q), .clk(CLOCK));  // open: clr
  Register #(.width(32)) R7 (.D(DATA_IN), .en(and_8_out), .Q(R7_q), .clk(CLOCK));  // open: clr
  Register #(.width(32)) R8 (.D(DATA_IN), .en(and_9_out), .Q(R8_q), .clk(CLOCK));  // open: clr
  Register #(.width(32)) R9 (.D(DATA_IN), .en(and_10_out), .Q(R9_q), .clk(CLOCK));  // open: clr
  Register #(.width(32)) R10 (.D(DATA_IN), .en(and_11_out), .Q(R10_q), .clk(CLOCK));  // open: clr
  Register #(.width(32)) R11 (.D(DATA_IN), .en(and_12_out), .Q(R11_q), .clk(CLOCK));  // open: clr
  Register #(.width(32)) R12 (.D(DATA_IN), .en(and_13_out), .Q(R12_q), .clk(CLOCK));  // open: clr
  Register #(.width(32)) R13 (.D(DATA_IN), .en(and_14_out), .Q(R13_q), .clk(CLOCK));  // open: clr
  Register #(.width(32)) R14 (.D(DATA_IN), .en(and_15_out), .Q(R14_q), .clk(CLOCK));  // open: clr
  Register #(.width(32)) R15 (.D(DATA_IN), .en(and_16_out), .Q(R15_q), .clk(CLOCK));  // open: clr
  Decoder #(.select(4), .enable("false")) decoder_2 (
    .out0(decoder_2_out0), .out1(decoder_2_out1), .out2(decoder_2_out2), .out3(decoder_2_out3),
    .out4(decoder_2_out4), .out5(decoder_2_out5), .out6(decoder_2_out6), .out7(decoder_2_out7),
    .out8(decoder_2_out8), .out9(decoder_2_out9), .out10(decoder_2_out10), .out11(decoder_2_out11),
    .out12(decoder_2_out12), .out13(decoder_2_out13), .out14(decoder_2_out14), .out15(decoder_2_out15),
    .sel(SRC1_REG));
  assign SRC1_OUT = decoder_2_out0 ? multiplexer_1_out : 32'bz;  // Controlled_Buffer controlled_buffer_1
  assign SRC1_OUT = decoder_2_out1 ? R1_q : 32'bz;  // Controlled_Buffer controlled_buffer_2
  assign SRC1_OUT = decoder_2_out2 ? R2_q : 32'bz;  // Controlled_Buffer controlled_buffer_3
  assign SRC1_OUT = decoder_2_out3 ? R3_q : 32'bz;  // Controlled_Buffer controlled_buffer_4
  assign SRC1_OUT = decoder_2_out4 ? R4_q : 32'bz;  // Controlled_Buffer controlled_buffer_5
  assign SRC1_OUT = decoder_2_out5 ? R5_q : 32'bz;  // Controlled_Buffer controlled_buffer_6
  assign SRC1_OUT = decoder_2_out6 ? R6_q : 32'bz;  // Controlled_Buffer controlled_buffer_7
  assign SRC1_OUT = decoder_2_out7 ? R7_q : 32'bz;  // Controlled_Buffer controlled_buffer_8
  assign SRC1_OUT = decoder_2_out8 ? R8_q : 32'bz;  // Controlled_Buffer controlled_buffer_9
  assign SRC1_OUT = decoder_2_out9 ? R9_q : 32'bz;  // Controlled_Buffer controlled_buffer_10
  assign SRC1_OUT = decoder_2_out10 ? R10_q : 32'bz;  // Controlled_Buffer controlled_buffer_11
  assign SRC1_OUT = decoder_2_out11 ? R11_q : 32'bz;  // Controlled_Buffer controlled_buffer_12
  assign SRC1_OUT = decoder_2_out12 ? R12_q : 32'bz;  // Controlled_Buffer controlled_buffer_13
  assign SRC1_OUT = decoder_2_out13 ? R13_q : 32'bz;  // Controlled_Buffer controlled_buffer_14
  assign SRC1_OUT = decoder_2_out14 ? R14_q : 32'bz;  // Controlled_Buffer controlled_buffer_15
  assign SRC1_OUT = decoder_2_out15 ? R15_q : 32'bz;  // Controlled_Buffer controlled_buffer_16
  Decoder #(.select(4), .enable("false")) decoder_3 (
    .out0(decoder_3_out0), .out1(decoder_3_out1), .out2(decoder_3_out2), .out3(decoder_3_out3),
    .out4(decoder_3_out4), .out5(decoder_3_out5), .out6(decoder_3_out6), .out7(decoder_3_out7),
    .out8(decoder_3_out8), .out9(decoder_3_out9), .out10(decoder_3_out10), .out11(decoder_3_out11),
    .out12(decoder_3_out12), .out13(decoder_3_out13), .out14(decoder_3_out14), .out15(decoder_3_out15),
    .sel(SRC2_REG));
  assign SRC2_OUT = decoder_3_out0 ? multiplexer_1_out : 32'bz;  // Controlled_Buffer controlled_buffer_17
  assign SRC2_OUT = decoder_3_out1 ? R1_q : 32'bz;  // Controlled_Buffer controlled_buffer_18
  assign SRC2_OUT = decoder_3_out2 ? R2_q : 32'bz;  // Controlled_Buffer controlled_buffer_19
  assign SRC2_OUT = decoder_3_out3 ? R3_q : 32'bz;  // Controlled_Buffer controlled_buffer_20
  assign SRC2_OUT = decoder_3_out4 ? R4_q : 32'bz;  // Controlled_Buffer controlled_buffer_21
  assign SRC2_OUT = decoder_3_out5 ? R5_q : 32'bz;  // Controlled_Buffer controlled_buffer_22
  assign SRC2_OUT = decoder_3_out6 ? R6_q : 32'bz;  // Controlled_Buffer controlled_buffer_23
  assign SRC2_OUT = decoder_3_out7 ? R7_q : 32'bz;  // Controlled_Buffer controlled_buffer_24
  assign SRC2_OUT = decoder_3_out8 ? R8_q : 32'bz;  // Controlled_Buffer controlled_buffer_25
  assign SRC2_OUT = decoder_3_out9 ? R9_q : 32'bz;  // Controlled_Buffer controlled_buffer_26
  assign SRC2_OUT = decoder_3_out10 ? R10_q : 32'bz;  // Controlled_Buffer controlled_buffer_27
  assign SRC2_OUT = decoder_3_out11 ? R11_q : 32'bz;  // Controlled_Buffer controlled_buffer_28
  assign SRC2_OUT = decoder_3_out12 ? R12_q : 32'bz;  // Controlled_Buffer controlled_buffer_29
  assign SRC2_OUT = decoder_3_out13 ? R13_q : 32'bz;  // Controlled_Buffer controlled_buffer_30
  assign SRC2_OUT = decoder_3_out14 ? R14_q : 32'bz;  // Controlled_Buffer controlled_buffer_31
  assign SRC2_OUT = decoder_3_out15 ? R15_q : 32'bz;  // Controlled_Buffer controlled_buffer_32
endmodule
