// Logisim project pipe.circ as structural Verilog: 1 circuit, main circuit main
module main (
  input  [3:0] in_1
);

  wire clock_1_out;
  wire [3:0] counter_1_q, multiplexer_1_out, register_1_q, register_2_q;

  Clock clock_1 (.out(clock_1_out));
  Counter #(.width(4), .max('hf)) counter_1 (.Q(counter_1_q), .clk(clock_1_out));  // open: load, D, count, carry, clr
  // Probe on register_1_q
  Register #(.width(4)) register_1 (.D(counter_1_q), .Q(register_1_q), .clk(clock_1_out));  // open: en, clr
  Multiplexer #(.width(4), .enable("false")) multiplexer_1 (
    .in0(register_1_q), .in1(4'b0000), .out(multiplexer_1_out), .sel(register_1_q[2]));
  // Probe on register_2_q
  Register #(.width(4)) register_2 (.D(multiplexer_1_out), .Q(register_2_q), .clk(clock_1_out));  // open: en, clr
endmodule
