// Logisim project clock1.circ as structural Verilog: 3 circuits, main circuit main
module main (
  input  [3:0] in_1
);

  wire and_1_out, clock_1_out, controlled_buffer_1_out, down2_1_c, down_1_c, xnor_1_out;
  wire [3:0] down2_1_out, down_1_out;

  Clock clock_1 (.out(clock_1_out));
  assign controlled_buffer_1_out = xnor_1_out ? clock_1_out : 1'bz;  // Controlled_Buffer controlled_buffer_1
  xnor xnor_1 (xnor_1_out, down_1_c, down2_1_c);
  down down_1 (.en(and_1_out), .out(down_1_out), .c(down_1_c));
  and and_1 (and_1_out, clock_1_out, down2_1_c);
  down2 down2_1 (.en(controlled_buffer_1_out), .out(down2_1_out), .c(down2_1_c));  // open: in
  LED led_1 (.in(down_1_c));
  DotMatrix #(.matrixcols(1), .matrixrows(4)) dotmatrix_1 (.col0(down_1_out));
  DotMatrix #(.matrixcols(1), .matrixrows(4)) dotmatrix_2 (.col0(down2_1_out));
endmodule

module down (
  input  en,
  output [3:0] out,
  output c
);

  wire [3:0] bit_extender_1_out;

  assign bit_extender_1_out = {{3{1'b1}}, 1'b1};  // Bit_Extender bit_extender_1
  Counter #(.width(4), .max('hf)) counter_1 (
    .load(1'b1), .D(bit_extender_1_out), .Q(out), .carry(c), .clk(en));  // open: count, clr
endmodule

module down2 (
  input  [3:0] in,
  input  en,
  output [3:0] out,
  output c
);

  wire clock_1_out;

  Clock clock_1 (.out(clock_1_out));
  Counter #(.width(4), .max('hf)) counter_1 (
    .load(1'b1), .D(in), .Q(out), .carry(c), .clk(clock_1_out));  // open: count, clr
endmodule
