// Logisim project cpu.circ as structural Verilog: 23 circuits, main circuit main
module main (
  input  [3:0] ALU_op,
  input  [1:0] A_src,
  input  [1:0] B_src,
  input  C_write,
  input  data_src,
  input  X_write,
  input  [1:0] addr_src,
  input  [1:0] ACCUM_src,
  input  ACCUM_write,
  input  oper_write,
  input  IR_write,
  input  PC_write,
  input  mem_write
);

  wire alu_old_1_c_out, alu_old_1_n, alu_old_1_v, alu_old_1_z, CLOCK_out, d_ff_1_q, not_1_out;
  wire [7:0] STATE_q;
  wire [15:0] ACCUM_q, alu_old_1_result, IR_q, multiplexer_1_out, multiplexer_2_out, multiplexer_3_out,
       multiplexer_4_out, multiplexer_5_out, OPER_q, PC_q, ram_1_data, rom_1_data, X_q;

  Clock CLOCK (.out(CLOCK_out));
  Register #(.width(16)) PC (.D(alu_old_1_result), .en(PC_write), .Q(PC_q), .clk(CLOCK_out));  // open: clr
  Register STATE (.Q(STATE_q), .clk(CLOCK_out));  // open: D, en, clr
  Multiplexer #(.select(2), .width(16)) multiplexer_1 (
    .in0(ACCUM_q), .in1(PC_q), .out(multiplexer_1_out), .sel(A_src));  // open: in2, in3
  Multiplexer #(.width(16)) multiplexer_2 (
    .in0(ACCUM_q), .in1(alu_old_1_result), .out(multiplexer_2_out), .sel(data_src));
  Multiplexer #(.select(2), .width(16)) multiplexer_3 (
    .in0(PC_q), .in1(OPER_q), .out(multiplexer_3_out), .sel(addr_src));  // open: in2, in3
  RAM #(.addrWidth(16), .dataWidth(16), .bus("separate")) ram_1 (
    .addr(multiplexer_3_out), .din(multiplexer_2_out), .data(ram_1_data), .str(mem_write), .clk(CLOCK_out),
    .ld(not_1_out));  // open: sel, clr
  not not_1 (not_1_out, mem_write);
  ROM #(.dataWidth(16)) rom_1 (.addr(STATE_q), .data(rom_1_data));  // open: sel
  Multiplexer #(.select(2), .width(16)) multiplexer_4 (
    .in0({16{1'b0}}), .in1(16'h1), .in2(OPER_q), .out(multiplexer_4_out), .sel(B_src));  // open: in3
  Register #(.width(16)) OPER (.D(ram_1_data), .en(oper_write), .Q(OPER_q), .clk(CLOCK_out));  // open: clr
  alu_old alu_old_1 (
    .oper(ALU_op), .A(multiplexer_1_out), .B(multiplexer_4_out), .C_in(d_ff_1_q), .Z(alu_old_1_z),
    .Result(alu_old_1_result), .C_out(alu_old_1_c_out), .N(alu_old_1_n), .V(alu_old_1_v));  // open: out_8
  Register #(.width(16)) IR (.D(ram_1_data), .en(IR_write), .Q(IR_q), .clk(CLOCK_out));  // open: clr
  Multiplexer #(.select(2), .width(16)) multiplexer_5 (
    .in0(ram_1_data), .in1(alu_old_1_result), .out(multiplexer_5_out), .sel(ACCUM_src));  // open: in2, in3
  Register #(.width(16)) ACCUM (.D(multiplexer_5_out), .en(ACCUM_write), .Q(ACCUM_q), .clk(CLOCK_out));  // open: clr
  D_Flip_Flop d_ff_1 (.clk(CLOCK_out), .D(alu_old_1_c_out), .Q(d_ff_1_q), .en(C_write));  // open: Qn, preset, reset
  Register #(.width(16)) X (.D(ram_1_data), .en(X_write), .Q(X_q), .clk(CLOCK_out));  // open: clr

  // Notes on the sheet:
  //   contents of rom_1 (hex, n*v repeats v):
  //   c000
endmodule

module alu_old (
  input  [3:0] oper,
  input  [15:0] A,
  input  [15:0] B,
  input  C_in,
  output Z,
  output [15:0] Result,
  output C_out,
  output [15:0] out_8,
  output N,
  output V
);

  wire adder_1_cout, subtractor_1_bout;
  wire [15:0] adder_1_out, subtractor_1_out;

  Adder #(.width(16)) adder_1 (.a(B), .b(A), .out(adder_1_out), .cin(C_in), .cout(adder_1_cout));
  Subtractor #(.width(16)) subtractor_1 (.a(A), .b(B), .out(subtractor_1_out), .bin(C_in), .bout(subtractor_1_bout));
  ExactlyOne xor_1[15:0] (.out(out_8), .in0(adder_1_out), .in1(A), .in2(B));
  Multiplexer #(.select(4), .width(16)) multiplexer_1 (
    .in0(adder_1_out), .in1(subtractor_1_out), .out({N, Result[14:0]}), .sel(oper));  // open: in2, in3, in4, in5, in6, in7, in8, in9, in10, in11, in12, in13, in14, in15
  Multiplexer #(.select(4)) multiplexer_2 (
    .in0(adder_1_cout), .in1(subtractor_1_bout), .out(C_out), .sel(oper));  // open: in2, in3, in4, in5, in6, in7, in8, in9, in10, in11, in12, in13, in14, in15
  Pull_Resistor pull_resistor_1 (.node({N, Result[14:0]}));
  nor nor_1 (Z, Result[0], Result[1], Result[2], Result[3], Result[4], Result[5], Result[6], Result[7], Result[8], Result[9], Result[10], Result[11], Result[12], Result[13], Result[14], N);
  Pull_Resistor pull_resistor_2 (.node(C_out));
  overflow overflow_1 (.a(A[15]), .b(B[15]), .r(N), .v(V));
  Pull_Resistor pull_resistor_3 (.node(V));

  assign Result[15] = N;

  // Notes on the sheet:
  //   add adc, sbc and disable carry for add and sub
endmodule

module overflow (
  input  a,
  input  b,
  input  r,
  output v
);

  wire and_1_out, and_2_out, and_3_out, and_4_out, not_1_out, not_2_out, not_3_out;

  not not_1 (not_1_out, a);
  not not_2 (not_2_out, b);
  and and_1 (and_1_out, not_1_out, not_2_out);
  and and_2 (and_2_out, a, b);
  not not_3 (not_3_out, r);
  and and_3 (and_3_out, and_1_out, r);
  and and_4 (and_4_out, and_2_out, not_3_out);
  or or_1 (v, and_3_out, and_4_out);
endmodule

module \reg  (
  input  r0_zero,
  input  clock,
  input  reg_write,
  input  [3:0] dst_reg,
  input  [3:0] src_reg,
  input  [15:0] data_in,
  input  src_reg_bus,
  output [15:0] src_out,
  output [15:0] dst_out,
  output [15:0] data_out
);

  wire and_1_out, and_2_out, and_3_out, and_4_out, and_5_out, and_6_out, and_7_out, and_8_out, and_9_out,
       and_10_out, and_11_out, and_12_out, and_13_out, and_14_out, and_15_out, and_16_out, and_17_out,
       and_18_out, and_19_out, and_20_out, and_21_out, and_22_out, and_23_out, and_24_out, and_25_out,
       and_26_out, and_27_out, and_28_out, and_29_out, and_30_out, and_31_out, and_32_out, decoder_1_out0,
       decoder_1_out1, decoder_1_out2, decoder_1_out3, decoder_1_out4, decoder_1_out5, decoder_1_out6,
       decoder_1_out7, decoder_1_out8, decoder_1_out9, decoder_1_out10, decoder_1_out11, decoder_1_out12,
       decoder_1_out13, decoder_1_out14, decoder_1_out15, decoder_2_out0, decoder_2_out1, decoder_2_out2,
       decoder_2_out3, decoder_2_out4, decoder_2_out5, decoder_2_out6, decoder_2_out7, decoder_2_out8,
       decoder_2_out9, decoder_2_out10, decoder_2_out11, decoder_2_out12, decoder_2_out13, decoder_2_out14,
       decoder_2_out15, not_1_out;
  wire [15:0] controlled_buffer_1_out, controlled_buffer_2_out, controlled_buffer_3_out,
       controlled_buffer_4_out, controlled_buffer_5_out, controlled_buffer_6_out, controlled_buffer_7_out,
       controlled_buffer_8_out, controlled_buffer_9_out, controlled_buffer_10_out, controlled_buffer_11_out,
       controlled_buffer_12_out, controlled_buffer_13_out, controlled_buffer_14_out,
       controlled_buffer_15_out, controlled_buffer_16_out, multiplexer_1_out, r0_q, r1_q, r2_q, r3_q, r4_q,
       r5_q, r6_q, r7_q, r8_q, r9_q, r10_q, r11_q, r12_q, r13_q, r14_q, r15_q;

  Decoder #(.select(4)) decoder_1 (
    .out0(decoder_1_out0), .out1(decoder_1_out1), .out2(decoder_1_out2), .out3(decoder_1_out3),
    .out4(decoder_1_out4), .out5(decoder_1_out5), .out6(decoder_1_out6), .out7(decoder_1_out7),
    .out8(decoder_1_out8), .out9(decoder_1_out9), .out10(decoder_1_out10), .out11(decoder_1_out11),
    .out12(decoder_1_out12), .out13(decoder_1_out13), .out14(decoder_1_out14), .out15(decoder_1_out15),
    .sel(dst_reg));
  and and_1 (and_1_out, decoder_1_out0, reg_write);
  and and_2 (and_2_out, decoder_1_out1, reg_write);
  and and_3 (and_3_out, decoder_1_out2, reg_write);
  and and_4 (and_4_out, decoder_1_out3, reg_write);
  and and_5 (and_5_out, decoder_1_out4, reg_write);
  and and_6 (and_6_out, decoder_1_out5, reg_write);
  and and_7 (and_7_out, decoder_1_out6, reg_write);
  and and_8 (and_8_out, decoder_1_out7, reg_write);
  and and_9 (and_9_out, decoder_1_out8, reg_write);
  and and_10 (and_10_out, decoder_1_out9, reg_write);
  and and_11 (and_11_out, decoder_1_out10, reg_write);
  and and_12 (and_12_out, decoder_1_out11, reg_write);
  and and_13 (and_13_out, decoder_1_out12, reg_write);
  and and_14 (and_14_out, decoder_1_out13, reg_write);
  and and_15 (and_15_out, decoder_1_out14, reg_write);
  and and_16 (and_16_out, decoder_1_out15, reg_write);
  Multiplexer #(.width(16)) multiplexer_1 (
    .in0(controlled_buffer_1_out), .in1({16{1'b0}}), .out(multiplexer_1_out), .sel(r0_zero));
  assign controlled_buffer_1_out = decoder_1_out0 ? data_out : 16'bz;  // Controlled_Buffer controlled_buffer_1
  Register #(.width(16)) r0 (.D(multiplexer_1_out), .en(and_1_out), .Q(r0_q), .clk(clock));  // open: clr
  assign controlled_buffer_2_out = decoder_1_out1 ? data_out : 16'bz;  // Controlled_Buffer controlled_buffer_2
  Register #(.width(16)) r1 (.D(controlled_buffer_2_out), .en(and_2_out), .Q(r1_q), .clk(clock));  // open: clr
  Register #(.width(16)) r2 (.D(controlled_buffer_3_out), .en(and_3_out), .Q(r2_q), .clk(clock));  // open: clr
  Register #(.width(16)) r3 (.D(controlled_buffer_4_out), .en(and_4_out), .Q(r3_q), .clk(clock));  // open: clr
  Register #(.width(16)) r4 (.D(controlled_buffer_5_out), .en(and_5_out), .Q(r4_q), .clk(clock));  // open: clr
  Register #(.width(16)) r5 (.D(controlled_buffer_6_out), .en(and_6_out), .Q(r5_q), .clk(clock));  // open: clr
  Register #(.width(16)) r6 (.D(controlled_buffer_7_out), .en(and_7_out), .Q(r6_q), .clk(clock));  // open: clr
  Register #(.width(16)) r7 (.D(controlled_buffer_8_out), .en(and_8_out), .Q(r7_q), .clk(clock));  // open: clr
  Register #(.width(16)) r8 (.D(controlled_buffer_9_out), .en(and_9_out), .Q(r8_q), .clk(clock));  // open: clr
  Register #(.width(16)) r9 (.D(controlled_buffer_10_out), .en(and_10_out), .Q(r9_q), .clk(clock));  // open: clr
  Register #(.width(16)) r10 (.D(controlled_buffer_11_out), .en(and_11_out), .Q(r10_q), .clk(clock));  // open: clr
  Register #(.width(16)) r11 (.D(controlled_buffer_12_out), .en(and_12_out), .Q(r11_q), .clk(clock));  // open: clr
  Register #(.width(16)) r12 (.D(controlled_buffer_13_out), .en(and_13_out), .Q(r12_q), .clk(clock));  // open: clr
  Register #(.width(16)) r13 (.D(controlled_buffer_14_out), .en(and_14_out), .Q(r13_q), .clk(clock));  // open: clr
  Register #(.width(16)) r14 (.D(controlled_buffer_15_out), .en(and_15_out), .Q(r14_q), .clk(clock));  // open: clr
  Register #(.width(16)) r15 (.D(controlled_buffer_16_out), .en(and_16_out), .Q(r15_q), .clk(clock));  // open: clr
  assign controlled_buffer_3_out = decoder_1_out2 ? data_out : 16'bz;  // Controlled_Buffer controlled_buffer_3
  assign controlled_buffer_4_out = decoder_1_out3 ? data_out : 16'bz;  // Controlled_Buffer controlled_buffer_4
  assign controlled_buffer_5_out = decoder_1_out4 ? data_out : 16'bz;  // Controlled_Buffer controlled_buffer_5
  assign controlled_buffer_6_out = decoder_1_out5 ? data_out : 16'bz;  // Controlled_Buffer controlled_buffer_6
  assign controlled_buffer_7_out = decoder_1_out6 ? data_out : 16'bz;  // Controlled_Buffer controlled_buffer_7
  assign controlled_buffer_8_out = decoder_1_out7 ? data_out : 16'bz;  // Controlled_Buffer controlled_buffer_8
  assign controlled_buffer_9_out = decoder_1_out8 ? data_out : 16'bz;  // Controlled_Buffer controlled_buffer_9
  assign controlled_buffer_10_out = decoder_1_out9 ? data_out : 16'bz;  // Controlled_Buffer controlled_buffer_10
  assign controlled_buffer_11_out = decoder_1_out10 ? data_out : 16'bz;  // Controlled_Buffer controlled_buffer_11
  assign controlled_buffer_12_out = decoder_1_out11 ? data_out : 16'bz;  // Controlled_Buffer controlled_buffer_12
  assign controlled_buffer_13_out = decoder_1_out12 ? data_out : 16'bz;  // Controlled_Buffer controlled_buffer_13
  assign controlled_buffer_14_out = decoder_1_out13 ? data_out : 16'bz;  // Controlled_Buffer controlled_buffer_14
  Decoder #(.select(4)) decoder_2 (
    .out0(decoder_2_out0), .out1(decoder_2_out1), .out2(decoder_2_out2), .out3(decoder_2_out3),
    .out4(decoder_2_out4), .out5(decoder_2_out5), .out6(decoder_2_out6), .out7(decoder_2_out7),
    .out8(decoder_2_out8), .out9(decoder_2_out9), .out10(decoder_2_out10), .out11(decoder_2_out11),
    .out12(decoder_2_out12), .out13(decoder_2_out13), .out14(decoder_2_out14), .out15(decoder_2_out15),
    .sel(src_reg));
  assign controlled_buffer_15_out = decoder_1_out14 ? data_out : 16'bz;  // Controlled_Buffer controlled_buffer_15
  assign controlled_buffer_16_out = decoder_1_out15 ? data_out : 16'bz;  // Controlled_Buffer controlled_buffer_16
  Multiplexer #(.select(4), .width(16)) multiplexer_2 (
    .in0(r0_q), .in1(r1_q), .in2(r2_q), .in3(r3_q), .in4(r4_q), .in5(r5_q), .in6(r6_q), .in7(r7_q),
    .in8(r8_q), .in9(r9_q), .in10(r10_q), .in11(r11_q), .in12(r12_q), .in13(r13_q), .in14(r14_q),
    .in15(r15_q), .out(src_out), .sel(src_reg));
  Multiplexer #(.select(4), .width(16)) multiplexer_3 (
    .in0(r0_q), .in1(r1_q), .in2(r2_q), .in3(r3_q), .in4(r4_q), .in5(r5_q), .in6(r6_q), .in7(r7_q),
    .in8(r8_q), .in9(r9_q), .in10(r10_q), .in11(r11_q), .in12(r12_q), .in13(r13_q), .in14(r14_q),
    .in15(r15_q), .out(dst_out), .sel(dst_reg));
  assign data_out = and_30_out ? r13_q : 16'bz;  // Controlled_Buffer controlled_buffer_17
  assign data_out = and_31_out ? r14_q : 16'bz;  // Controlled_Buffer controlled_buffer_18
  assign data_out = and_32_out ? r15_q : 16'bz;  // Controlled_Buffer controlled_buffer_19
  assign data_out = and_26_out ? r9_q : 16'bz;  // Controlled_Buffer controlled_buffer_20
  assign data_out = and_27_out ? r10_q : 16'bz;  // Controlled_Buffer controlled_buffer_21
  assign data_out = and_28_out ? r11_q : 16'bz;  // Controlled_Buffer controlled_buffer_22
  assign data_out = and_29_out ? r12_q : 16'bz;  // Controlled_Buffer controlled_buffer_23
  assign data_out = and_22_out ? r5_q : 16'bz;  // Controlled_Buffer controlled_buffer_24
  assign data_out = and_23_out ? r6_q : 16'bz;  // Controlled_Buffer controlled_buffer_25
  assign data_out = and_24_out ? r7_q : 16'bz;  // Controlled_Buffer controlled_buffer_26
  assign data_out = and_25_out ? r8_q : 16'bz;  // Controlled_Buffer controlled_buffer_27
  assign data_out = src_reg_bus ? data_in : 16'bz;  // Controlled_Buffer controlled_buffer_28
  assign data_out = and_18_out ? r1_q : 16'bz;  // Controlled_Buffer controlled_buffer_29
  assign data_out = and_19_out ? r2_q : 16'bz;  // Controlled_Buffer controlled_buffer_30
  assign data_out = and_20_out ? r3_q : 16'bz;  // Controlled_Buffer controlled_buffer_31
  assign data_out = and_21_out ? r4_q : 16'bz;  // Controlled_Buffer controlled_buffer_32
  assign data_out = and_17_out ? r0_q : 16'bz;  // Controlled_Buffer controlled_buffer_33
  not not_1 (not_1_out, src_reg_bus);
  and and_17 (and_17_out, decoder_2_out0, not_1_out);
  and and_18 (and_18_out, decoder_2_out1, not_1_out);
  and and_19 (and_19_out, decoder_2_out2, not_1_out);
  and and_20 (and_20_out, decoder_2_out3, not_1_out);
  and and_21 (and_21_out, decoder_2_out4, not_1_out);
  and and_22 (and_22_out, decoder_2_out5, not_1_out);
  and and_23 (and_23_out, decoder_2_out6, not_1_out);
  and and_24 (and_24_out, decoder_2_out7, not_1_out);
  and and_25 (and_25_out, decoder_2_out8, not_1_out);
  and and_26 (and_26_out, decoder_2_out9, not_1_out);
  and and_27 (and_27_out, decoder_2_out10, not_1_out);
  and and_28 (and_28_out, decoder_2_out11, not_1_out);
  and and_29 (and_29_out, decoder_2_out12, not_1_out);
  and and_30 (and_30_out, decoder_2_out13, not_1_out);
  and and_31 (and_31_out, decoder_2_out14, not_1_out);
  and and_32 (and_32_out, decoder_2_out15, not_1_out);
endmodule

module alu (
  input  [3:0] oper,
  input  [15:0] A,
  input  [15:0] B,
  input  C_in,
  output Z,
  output [15:0] Result,
  output C_out,
  output N,
  output V
);

  wire adder_1_cout, subtractor_1_bout;
  wire [15:0] adder_1_out, subtractor_1_out, xor_1_out;

  Adder #(.width(16)) adder_1 (.a(B), .b(A), .out(adder_1_out), .cin(C_in), .cout(adder_1_cout));
  Subtractor #(.width(16)) subtractor_1 (.a(A), .b(B), .out(subtractor_1_out), .bin(C_in), .bout(subtractor_1_bout));
  ExactlyOne xor_1[15:0] (.out(xor_1_out), .in0(adder_1_out), .in1(A), .in2(B));
  // Probe on xor_1_out
  Multiplexer #(.select(4), .width(16)) multiplexer_1 (
    .in0(adder_1_out), .in1(subtractor_1_out), .out({N, Result[14:0]}), .sel(oper));  // open: in2, in3, in4, in5, in6, in7, in8, in9, in10, in11, in12, in13, in14, in15
  Multiplexer #(.select(4)) multiplexer_2 (
    .in0(adder_1_cout), .in1(subtractor_1_bout), .out(C_out), .sel(oper));  // open: in2, in3, in4, in5, in6, in7, in8, in9, in10, in11, in12, in13, in14, in15
  Pull_Resistor pull_resistor_1 (.node({N, Result[14:0]}));
  nor nor_1 (Z, Result[0], Result[1], Result[2], Result[3], Result[4], Result[5], Result[6], Result[7], Result[8], Result[9], Result[10], Result[11], Result[12], Result[13], Result[14], N);
  Pull_Resistor pull_resistor_2 (.node(C_out));
  overflow overflow_1 (.a(A[15]), .b(B[15]), .r(N), .v(V));
  Pull_Resistor pull_resistor_3 (.node(V));

  assign Result[15] = N;

  // Notes on the sheet:
  //   add adc, sbc and disable carry for add and sub
endmodule

module cpu (
  input  REG_write,
  input  [1:0] A_src,
  input  [1:0] B_src,
  input  reg_data,
  input  EA_reg_src,
  input  [1:0] MEM_data_src,
  input  [1:0] REG_DATA_src,
  input  MAR_write,
  input  [1:0] A_src_2,
  input  ADDR_src,
  input  TEMP_write,
  input  OPER_write,
  input  IR_write,
  input  PC_write,
  input  MEM_write
);

  wire CLOCK_out, not_1_out, undriven;
  wire [3:0] IR_q_2, IR_q_3;
  wire [10:0] IR_q;
  wire [15:0] adder_1_out, adder_2_out, alu_1_result, MAR_q, multiplexer_1_out, multiplexer_2_out,
       multiplexer_3_out, multiplexer_4_out, multiplexer_5_out, multiplexer_6_out, multiplexer_7_out, OPER_q,
       PC_q, ram_1_data, reg_1_dst_out, reg_1_src_out, TEMP_q;
  wire [15:15] IR_q_4;

  Clock CLOCK (.out(CLOCK_out));
  Multiplexer #(.width(16)) multiplexer_1 (
    .in0(reg_1_src_out), .in1(reg_1_dst_out), .out(multiplexer_1_out), .sel(EA_reg_src));
  Adder #(.width(16)) adder_1 (.a(PC_q), .b(16'h1), .out(adder_1_out));  // open: cin, cout
  // Probe on adder_2_out
  Adder #(.width(16)) adder_2 (.a(multiplexer_1_out), .b(OPER_q), .out(adder_2_out));  // open: cin, cout
  Register #(.width(16)) PC (.D(adder_1_out), .en(PC_write), .Q(PC_q), .clk(CLOCK_out));  // open: clr
  Multiplexer #(.width(16)) multiplexer_2 (.in0(PC_q), .in1(MAR_q), .out(multiplexer_2_out), .sel(ADDR_src));
  Multiplexer #(.select(2), .width(16)) multiplexer_3 (
    .in0(reg_1_src_out), .in1(TEMP_q), .out(multiplexer_3_out), .sel(MEM_data_src));  // open: in2, in3
  Register #(.width(16)) MAR (.D(adder_2_out), .en(MAR_write), .Q(MAR_q), .clk(CLOCK_out));  // open: clr
  Multiplexer #(.select(2), .width(16)) multiplexer_4 (
    .in0(reg_1_src_out), .in1(reg_1_dst_out), .in2(ram_1_data), .out(multiplexer_4_out), .sel(A_src));  // open: in3
  RAM #(.addrWidth(16), .dataWidth(16), .bus("separate")) ram_1 (
    .addr(multiplexer_2_out), .din(multiplexer_3_out), .data(ram_1_data), .str(MEM_write), .clk(CLOCK_out),
    .ld(not_1_out));  // open: sel, clr
  not not_1 (not_1_out, MEM_write);
  Multiplexer #(.select(2), .width(16)) multiplexer_5 (
    .in0(reg_1_src_out), .in1(reg_1_dst_out), .in2(ram_1_data), .out(multiplexer_5_out), .sel(B_src));  // open: in3
  alu alu_1 (
    .oper(IR_q_3), .A(multiplexer_4_out), .B(multiplexer_5_out), .C_in(undriven), .Result(alu_1_result));  // open: Z, C_out, N, V
  Register #(.width(16)) OPER (.D(ram_1_data), .en(OPER_write), .Q(OPER_q), .clk(CLOCK_out));  // open: clr
  // Probe on IR_q[3:0]
  Register #(.width(16)) IR (
    .D(ram_1_data), .en(IR_write), .Q({IR_q_4[15], IR_q_3, IR_q[10:8], IR_q_2, IR_q[3:0]}), .clk(CLOCK_out));  // open: clr
  \reg  reg_1 (
    .clock(CLOCK_out), .reg_write(REG_write), .src_reg(IR_q_2), .data_in(multiplexer_6_out),
    .src_reg_bus(reg_data), .dst_reg(IR_q[3:0]), .r0_zero(1'b1), .src_out(reg_1_src_out),
    .dst_out(reg_1_dst_out));  // open: data_out
  // Probe on IR_q_2
  Multiplexer #(.select(2), .width(16)) multiplexer_6 (
    .in0(OPER_q), .in1(ram_1_data), .in2(alu_1_result), .out(multiplexer_6_out), .sel(REG_DATA_src));  // open: in3
  Multiplexer #(.select(2), .width(16)) multiplexer_7 (
    .in0(reg_1_src_out), .in1(reg_1_dst_out), .in2(alu_1_result), .out(multiplexer_7_out), .sel(A_src_2));  // open: in3
  Register #(.width(16)) TEMP (.D(multiplexer_7_out), .en(TEMP_write), .Q(TEMP_q), .clk(CLOCK_out));  // open: clr
endmodule

module addressing (
  input  in_1,
  input  in_2,
  input  [15:0] oper,
  input  [1:0] in_4,
  input  in_5,
  input  in_6,
  input  in_7,
  input  [15:0] instruction
);

  wire addr_con2_1_datasrc, addr_con2_1_easrc, addr_con2_1_memwrt, addr_con2_1_regdata, addr_con2_1_regwrt,
       clock_1_out, not_1_out;
  wire [1:0] addr_con2_1_adrsrc;
  wire [15:0] adder_1_out, multiplexer_1_out, multiplexer_2_out, multiplexer_3_out, ram_1_data,
       reg_1_data_out, reg_1_dst_out, reg_1_src_out;

  Clock clock_1 (.out(clock_1_out));
  // Probe on instruction[15:11]
  Multiplexer #(.width(16)) multiplexer_1 (
    .in0(oper), .in1(ram_1_data), .out(multiplexer_1_out), .sel(addr_con2_1_datasrc));
  // Probe on instruction[10:8]
  \reg  reg_1 (
    .clock(clock_1_out), .reg_write(addr_con2_1_regwrt), .src_reg(instruction[7:4]),
    .data_in(multiplexer_1_out), .src_reg_bus(addr_con2_1_regdata), .data_out(reg_1_data_out),
    .dst_reg(instruction[3:0]), .r0_zero(1'b1), .src_out(reg_1_src_out), .dst_out(reg_1_dst_out));
  addr_con2 addr_con2_1 (
    .adr(instruction[10:8]), .memwrt(addr_con2_1_memwrt), .regwrt(addr_con2_1_regwrt),
    .adrsrc(addr_con2_1_adrsrc), .easrc(addr_con2_1_easrc), .datasrc(addr_con2_1_datasrc),
    .regdata(addr_con2_1_regdata));
  // Probe on reg_1_src_out
  // Probe on reg_1_dst_out
  Multiplexer #(.width(16)) multiplexer_2 (
    .in0(reg_1_src_out), .in1(reg_1_dst_out), .out(multiplexer_2_out), .sel(addr_con2_1_easrc));
  Adder #(.width(16)) adder_1 (.a(multiplexer_2_out), .b(oper), .out(adder_1_out));  // open: cin, cout
  Multiplexer #(.select(2), .width(16)) multiplexer_3 (
    .in0(reg_1_src_out), .in1(reg_1_dst_out), .in2(adder_1_out), .out(multiplexer_3_out),
    .sel(addr_con2_1_adrsrc));  // open: in3
  not not_1 (not_1_out, addr_con2_1_memwrt);
  RAM #(.addrWidth(16), .dataWidth(16), .bus("separate")) ram_1 (
    .addr(multiplexer_3_out), .din(reg_1_src_out), .data(ram_1_data), .str(addr_con2_1_memwrt),
    .clk(clock_1_out), .ld(not_1_out));  // open: sel, clr
endmodule

module addr_con2 (
  input  [2:0] adr,
  output memwrt,
  output regwrt,
  output [1:0] adrsrc,
  output easrc,
  output datasrc,
  output regdata
);

  wire and_1_out, and_2_out, and_5_out, and_6_out, and_7_out, and_8_out, and_9_out, and_10_out, and_12_out,
       and_13_out, and_14_out, not_1_out, not_2_out, not_3_out, not_4_out, not_5_out, not_6_out, not_7_out,
       not_8_out, not_9_out, not_10_out, not_11_out, or_3_out;

  and and_1 (and_1_out, adr[2], adr[0]);
  and and_2 (and_2_out, adr[2], adr[1]);
  not not_1 (not_1_out, adr[1]);
  not not_2 (not_2_out, adr[0]);
  and and_3 (adrsrc[1], adr[2], adr[1]);
  not not_3 (not_3_out, adr[1]);
  and and_4 (easrc, adr[2], adr[1]);
  not not_4 (not_4_out, adr[1]);
  not not_5 (not_5_out, adr[2]);
  not not_6 (not_6_out, adr[2]);
  not not_7 (not_7_out, adr[1]);
  or or_1 (memwrt, and_1_out, and_2_out);
  not not_8 (not_8_out, adr[2]);
  and and_5 (and_5_out, not_1_out, not_2_out);
  and and_6 (and_6_out, adr[2], not_3_out);
  not not_9 (not_9_out, adr[2]);
  and and_7 (and_7_out, adr[2], not_4_out);
  not not_10 (not_10_out, adr[0]);
  and and_8 (and_8_out, not_5_out, adr[0]);
  and and_9 (and_9_out, not_6_out, adr[1]);
  and and_10 (and_10_out, adr[2], not_7_out);
  not not_11 (not_11_out, adr[0]);
  or or_2 (regwrt, not_8_out, and_5_out);
  and and_11 (adrsrc[0], and_6_out, adr[0]);
  and and_12 (and_12_out, not_9_out, adr[0]);
  and and_13 (and_13_out, and_7_out, not_10_out);
  or or_3 (or_3_out, and_8_out, and_9_out);
  and and_14 (and_14_out, and_10_out, not_11_out);
  or or_4 (datasrc, and_12_out, and_13_out);
  or or_5 (regdata, or_3_out, and_14_out);
endmodule

module addr_alu (
  input  [3:0] in_1,
  input  [1:0] in_2,
  input  [1:0] in_3,
  input  in_4,
  input  in_5,
  input  in_6,
  input  [15:0] oper,
  input  [1:0] in_8,
  input  in_9,
  input  in_10,
  input  in_11,
  input  [15:0] instruction
);

  wire addr_con2_1_datasrc, addr_con2_1_easrc, addr_con2_1_memwrt, addr_con2_1_regdata, addr_con2_1_regwrt,
       clock_1_out, not_1_out;
  wire [1:0] addr_con2_1_adrsrc;
  wire [15:0] adder_1_out, alu_1_result, multiplexer_1_out, multiplexer_2_out, multiplexer_3_out,
       multiplexer_4_out, multiplexer_5_out, multiplexer_6_out, ram_1_data, reg_1_data_out, reg_1_dst_out,
       reg_1_src_out;

  Clock clock_1 (.out(clock_1_out));
  // Probe on instruction[15:11]
  Multiplexer #(.width(16)) multiplexer_1 (
    .in0(oper), .in1(ram_1_data), .out(multiplexer_1_out), .sel(addr_con2_1_datasrc));
  // Probe on instruction[10:8]
  \reg  reg_1 (
    .clock(clock_1_out), .reg_write(addr_con2_1_regwrt), .src_reg(instruction[7:4]),
    .data_in(multiplexer_1_out), .src_reg_bus(addr_con2_1_regdata), .data_out(reg_1_data_out),
    .dst_reg(instruction[3:0]), .r0_zero(1'b1), .src_out(reg_1_src_out), .dst_out(reg_1_dst_out));
  addr_con2 addr_con2_1 (
    .adr(instruction[10:8]), .memwrt(addr_con2_1_memwrt), .regwrt(addr_con2_1_regwrt),
    .adrsrc(addr_con2_1_adrsrc), .easrc(addr_con2_1_easrc), .datasrc(addr_con2_1_datasrc),
    .regdata(addr_con2_1_regdata));
  // Probe on reg_1_src_out
  // Probe on reg_1_dst_out
  Multiplexer #(.width(16)) multiplexer_2 (
    .in0(reg_1_src_out), .in1(reg_1_dst_out), .out(multiplexer_2_out), .sel(addr_con2_1_easrc));
  Adder #(.width(16)) adder_1 (.a(multiplexer_2_out), .b(oper), .out(adder_1_out));  // open: cin, cout
  Multiplexer #(.select(2), .width(16)) multiplexer_3 (
    .in0(reg_1_src_out), .in1(reg_1_dst_out), .in2(ram_1_data), .out(multiplexer_3_out), .sel(in_2));  // open: in3
  Multiplexer #(.select(2), .width(16)) multiplexer_4 (
    .in0(reg_1_src_out), .in1(reg_1_dst_out), .in2(ram_1_data), .out(multiplexer_4_out), .sel(in_3));  // open: in3
  Multiplexer #(.width(16)) multiplexer_5 (
    .in0(reg_1_src_out), .in1(alu_1_result), .out(multiplexer_5_out), .sel(in_4));
  Multiplexer #(.select(2), .width(16)) multiplexer_6 (
    .in0(reg_1_src_out), .in1(reg_1_dst_out), .in2(adder_1_out), .out(multiplexer_6_out),
    .sel(addr_con2_1_adrsrc));  // open: in3
  // Probe on addr_con2_1_adrsrc
  alu alu_1 (
    .oper(in_1), .A(multiplexer_3_out), .B(multiplexer_4_out), .Result(alu_1_result));  // open: C_in, Z, C_out, N, V
  not not_1 (not_1_out, addr_con2_1_memwrt);
  // Probe on alu_1_result
  RAM #(.addrWidth(16), .dataWidth(16), .bus("separate")) ram_1 (
    .addr(multiplexer_6_out), .din(multiplexer_5_out), .data(ram_1_data), .str(addr_con2_1_memwrt),
    .clk(clock_1_out), .ld(not_1_out));  // open: sel, clr
endmodule

module op_fetch (
  input  a2,
  input  a1,
  input  a0,
  output pcwrt,
  output opwrt
);

  wire and_1_out, and_2_out, not_1_out, not_2_out;

  not not_1 (not_1_out, a0);
  not not_2 (not_2_out, a0);
  and and_1 (and_1_out, a2, not_1_out);
  and and_2 (and_2_out, a2, not_2_out);
  or or_1 (pcwrt, a1, and_1_out);
  or or_2 (opwrt, a1, and_2_out);
endmodule

module seq (
);

  wire clock_1_out;
  wire [3:0] counter_1_q, register_1_q;
  wire [7:0] rom_1_data;

  Clock clock_1 (.out(clock_1_out));
  // Probe on counter_1_q
  Counter #(.width(4), .max('hf)) counter_1 (
    .Q(counter_1_q), .clk(clock_1_out), .clr(rom_1_data[7]));  // open: load, D, count, carry
  // Probe on register_1_q
  Register #(.width(4)) register_1 (.Q(register_1_q), .clk(clock_1_out), .clr(rom_1_data[0]));  // open: D, en
  // Probe on {register_1_q, counter_1_q}
  ROM rom_1 (.addr({register_1_q, counter_1_q}), .data(rom_1_data));  // open: sel
  // Probe on rom_1_data

  // Notes on the sheet:
  //   contents of rom_1 (hex, n*v repeats v):
  //   0 0 0 80
endmodule

module yeah (
);

  wire clock_1_out, decoder_1_out0, decoder_1_out1, decoder_1_out2, decoder_1_out3, decoder_1_out4,
       decoder_1_out5, decoder_1_out6, decoder_1_out7;
  wire [2:0] counter_1_q;

  Clock clock_1 (.out(clock_1_out));
  Counter #(.width(3), .max('h7)) counter_1 (.Q(counter_1_q), .clk(clock_1_out));  // open: load, D, count, carry, clr
  // Probe on counter_1_q
  Decoder #(.select(3)) decoder_1 (
    .out0(decoder_1_out0), .out1(decoder_1_out1), .out2(decoder_1_out2), .out3(decoder_1_out3),
    .out4(decoder_1_out4), .out5(decoder_1_out5), .out6(decoder_1_out6), .out7(decoder_1_out7),
    .sel(counter_1_q));
endmodule

module reg2 (
  input  [1:0] src1_reg,
  input  [1:0] src2_reg,
  input  clock,
  input  write,
  input  [15:0] data_in,
  input  [1:0] data_reg,
  output [15:0] src1_out,
  output [15:0] src2_out
);

  wire and_1_out, and_2_out, and_3_out, and_4_out, and_5_out, and_6_out, and_7_out, and_8_out, and_9_out,
       and_10_out, and_11_out, and_12_out, and_13_out, and_14_out, and_15_out, and_16_out, decoder_1_out0,
       decoder_1_out1, decoder_1_out2, decoder_1_out3, decoder_2_out0, decoder_2_out1, decoder_2_out2,
       decoder_2_out3, decoder_3_out0, decoder_3_out1, decoder_3_out2, decoder_3_out3, undriven, undriven_2,
       undriven_3, undriven_4, undriven_5, undriven_6, undriven_7, undriven_8, undriven_9, undriven_10,
       undriven_11, undriven_12, undriven_13, undriven_14, undriven_15, undriven_16, undriven_17, undriven_18;
  wire [15:0] controlled_buffer_1_out, controlled_buffer_2_out, controlled_buffer_3_out,
       controlled_buffer_4_out, controlled_buffer_5_out, controlled_buffer_6_out, controlled_buffer_7_out,
       controlled_buffer_8_out, controlled_buffer_9_out, controlled_buffer_10_out, controlled_buffer_11_out,
       controlled_buffer_12_out, controlled_buffer_13_out, controlled_buffer_14_out,
       controlled_buffer_15_out, controlled_buffer_16_out, R0_q, R1_q, R2_q, R3_q;

  Decoder #(.select(2)) decoder_1 (
    .out0(decoder_1_out0), .out1(decoder_1_out1), .out2(decoder_1_out2), .out3(decoder_1_out3), .sel(data_reg));
  assign controlled_buffer_1_out = decoder_1_out0 ? data_in : 16'bz;  // Controlled_Buffer controlled_buffer_1
  assign controlled_buffer_2_out = decoder_1_out1 ? data_in : 16'bz;  // Controlled_Buffer controlled_buffer_2
  assign controlled_buffer_3_out = decoder_1_out2 ? data_in : 16'bz;  // Controlled_Buffer controlled_buffer_3
  assign controlled_buffer_4_out = decoder_1_out3 ? data_in : 16'bz;  // Controlled_Buffer controlled_buffer_4
  Controlled_Buffer #(.width(16)) controlled_buffer_5 (.in(data_in), .out(controlled_buffer_5_out));  // open: en
  Controlled_Buffer #(.width(16)) controlled_buffer_6 (.in(data_in), .out(controlled_buffer_6_out));  // open: en
  Controlled_Buffer #(.width(16)) controlled_buffer_7 (.in(data_in), .out(controlled_buffer_7_out));  // open: en
  Controlled_Buffer #(.width(16)) controlled_buffer_8 (.in(data_in), .out(controlled_buffer_8_out));  // open: en
  assign controlled_buffer_9_out = undriven ? data_in : 16'bz;  // Controlled_Buffer controlled_buffer_9
  assign controlled_buffer_10_out = undriven_2 ? data_in : 16'bz;  // Controlled_Buffer controlled_buffer_10
  assign controlled_buffer_11_out = undriven_3 ? data_in : 16'bz;  // Controlled_Buffer controlled_buffer_11
  assign controlled_buffer_12_out = undriven_4 ? data_in : 16'bz;  // Controlled_Buffer controlled_buffer_12
  Controlled_Buffer #(.width(16)) controlled_buffer_13 (.in(data_in), .out(controlled_buffer_13_out));  // open: en
  Controlled_Buffer #(.width(16)) controlled_buffer_14 (.in(data_in), .out(controlled_buffer_14_out));  // open: en
  assign controlled_buffer_15_out = undriven_5 ? data_in : 16'bz;  // Controlled_Buffer controlled_buffer_15
  assign controlled_buffer_16_out = undriven_6 ? data_in : 16'bz;  // Controlled_Buffer controlled_buffer_16
  and and_1 (and_1_out, decoder_1_out0, write);
  and and_2 (and_2_out, decoder_1_out1, write);
  and and_3 (and_3_out, decoder_1_out2, write);
  and and_4 (and_4_out, decoder_1_out3, write);
  and and_5 (and_5_out, undriven_7, write);
  and and_6 (and_6_out, undriven_8, write);
  and and_7 (and_7_out, undriven_9, write);
  and and_8 (and_8_out, undriven_10, write);
  and and_9 (and_9_out, undriven_11, write);
  and and_10 (and_10_out, undriven_12, write);
  and and_11 (and_11_out, undriven_13, write);
  and and_12 (and_12_out, undriven_14, write);
  and and_13 (and_13_out, undriven_15, write);
  and and_14 (and_14_out, undriven_16, write);
  and and_15 (and_15_out, undriven_17, write);
  and and_16 (and_16_out, undriven_18, write);
  Register #(.width(16)) R0 (.D(controlled_buffer_1_out), .en(and_1_out), .Q(R0_q), .clk(clock));  // open: clr
  Register #(.width(16)) R1 (.D(controlled_buffer_2_out), .en(and_2_out), .Q(R1_q), .clk(clock));  // open: clr
  Register #(.width(16)) R2 (.D(controlled_buffer_3_out), .en(and_3_out), .Q(R2_q), .clk(clock));  // open: clr
  Register #(.width(16)) R3 (.D(controlled_buffer_4_out), .en(and_4_out), .Q(R3_q), .clk(clock));  // open: clr
  Register #(.width(16)) R4 (.D(controlled_buffer_5_out), .en(and_5_out), .clk(clock));  // open: Q, clr
  Register #(.width(16)) R5 (.D(controlled_buffer_6_out), .en(and_6_out), .clk(clock));  // open: Q, clr
  Register #(.width(16)) R6 (.D(controlled_buffer_7_out), .en(and_7_out), .clk(clock));  // open: Q, clr
  Register #(.width(16)) R7 (.D(controlled_buffer_8_out), .en(and_8_out), .clk(clock));  // open: Q, clr
  Register #(.width(16)) R8 (.D(controlled_buffer_9_out), .en(and_9_out), .clk(clock));  // open: Q, clr
  Register #(.width(16)) R9 (.D(controlled_buffer_10_out), .en(and_10_out), .clk(clock));  // open: Q, clr
  Register #(.width(16)) R10 (.D(controlled_buffer_11_out), .en(and_11_out), .clk(clock));  // open: Q, clr
  Register #(.width(16)) R11 (.D(controlled_buffer_12_out), .en(and_12_out), .clk(clock));  // open: Q, clr
  Register #(.width(16)) R12 (.D(controlled_buffer_13_out), .en(and_13_out), .clk(clock));  // open: Q, clr
  Register #(.width(16)) R13 (.D(controlled_buffer_14_out), .en(and_14_out), .clk(clock));  // open: Q, clr
  Register #(.width(16)) R14 (.D(controlled_buffer_15_out), .en(and_15_out), .clk(clock));  // open: Q, clr
  Register #(.width(16)) R15 (.D(controlled_buffer_16_out), .en(and_16_out), .clk(clock));  // open: Q, clr
  Decoder #(.select(2)) decoder_2 (
    .out0(decoder_2_out0), .out1(decoder_2_out1), .out2(decoder_2_out2), .out3(decoder_2_out3), .sel(src1_reg));
  assign src1_out = decoder_2_out0 ? R0_q : 16'bz;  // Controlled_Buffer controlled_buffer_17
  assign src1_out = decoder_2_out1 ? R1_q : 16'bz;  // Controlled_Buffer controlled_buffer_18
  assign src1_out = decoder_2_out2 ? R2_q : 16'bz;  // Controlled_Buffer controlled_buffer_19
  assign src1_out = decoder_2_out3 ? R3_q : 16'bz;  // Controlled_Buffer controlled_buffer_20
  Decoder #(.select(2)) decoder_3 (
    .out0(decoder_3_out0), .out1(decoder_3_out1), .out2(decoder_3_out2), .out3(decoder_3_out3), .sel(src2_reg));
  assign src2_out = decoder_3_out0 ? R0_q : 16'bz;  // Controlled_Buffer controlled_buffer_21
  assign src2_out = decoder_3_out1 ? R1_q : 16'bz;  // Controlled_Buffer controlled_buffer_22
  assign src2_out = decoder_3_out2 ? R2_q : 16'bz;  // Controlled_Buffer controlled_buffer_23
  assign src2_out = decoder_3_out3 ? R3_q : 16'bz;  // Controlled_Buffer controlled_buffer_24
endmodule

module reg2_test (
  input  in_1,
  input  [15:0] in_2,
  input  [3:0] in_3
);

  wire and_1_out, and_2_out, and_3_out, and_4_out, clock_1_out, decoder_1_out0, decoder_1_out1,
       decoder_1_out2, decoder_1_out3;
  wire [1:0] undriven_2, undriven_3, undriven_4, undriven_5, undriven_6, undriven_7, undriven_8, undriven_9;
  wire [15:0] reg2_1_src1_out, reg2_1_src2_out, reg2_2_src1_out, reg2_2_src2_out, reg2_3_src1_out,
       reg2_3_src2_out, reg2_4_src1_out, reg2_4_src2_out, undriven;

  Clock clock_1 (.out(clock_1_out));
  Decoder #(.select(2)) decoder_1 (
    .out0(decoder_1_out0), .out1(decoder_1_out1), .out2(decoder_1_out2), .out3(decoder_1_out3),
    .sel(in_3[3:2]));
  and and_1 (and_1_out, in_1, decoder_1_out0);
  and and_2 (and_2_out, in_1, decoder_1_out1);
  and and_3 (and_3_out, in_1, decoder_1_out2);
  and and_4 (and_4_out, in_1, decoder_1_out3);
  reg2 reg2_1 (
    .clock(clock_1_out), .write(and_1_out), .data_in(undriven), .data_reg(in_3[1:0]), .src1_reg(undriven_3),
    .src1_out(reg2_1_src1_out), .src2_reg(undriven_2), .src2_out(reg2_1_src2_out));
  reg2 reg2_2 (
    .clock(clock_1_out), .write(and_2_out), .data_in(undriven), .data_reg(in_3[1:0]), .src1_reg(undriven_5),
    .src1_out(reg2_2_src1_out), .src2_reg(undriven_4), .src2_out(reg2_2_src2_out));
  reg2 reg2_3 (
    .clock(clock_1_out), .write(and_3_out), .data_in(in_2), .data_reg(in_3[1:0]), .src1_reg(undriven_7),
    .src1_out(reg2_3_src1_out), .src2_reg(undriven_6), .src2_out(reg2_3_src2_out));
  reg2 reg2_4 (
    .clock(clock_1_out), .write(and_4_out), .data_in(undriven), .data_reg(in_3[1:0]), .src1_reg(undriven_9),
    .src1_out(reg2_4_src1_out), .src2_reg(undriven_8), .src2_out(reg2_4_src2_out));
endmodule

module adder (
  input  A,
  input  B,
  input  Cin,
  output S,
  output Cout
);

  wire and_1_out, and_2_out, xor_1_out;

  xor xor_1 (xor_1_out, A, B);
  and and_1 (and_1_out, A, B);
  xor xor_2 (S, xor_1_out, Cin);
  and and_2 (and_2_out, xor_1_out, Cin);
  or or_1 (Cout, and_1_out, and_2_out);
endmodule

module adder16 (
  input  Cin,
  input  [15:0] A,
  input  [15:0] B,
  output [15:0] S,
  output Cout
);

  wire adder_1_cout, adder_2_cout, adder_3_cout, adder_4_cout, adder_5_cout, adder_6_cout, adder_7_cout,
       adder_8_cout, adder_9_cout, adder_10_cout, adder_11_cout, adder_12_cout, adder_13_cout, adder_14_cout,
       adder_15_cout;

  adder adder_1 (.A(A[0]), .B(B[0]), .Cin(Cin), .S(S[0]), .Cout(adder_1_cout));
  adder adder_2 (.A(A[1]), .B(B[1]), .Cin(adder_1_cout), .S(S[1]), .Cout(adder_2_cout));
  adder adder_3 (.A(A[2]), .B(B[2]), .Cin(adder_2_cout), .S(S[2]), .Cout(adder_3_cout));
  adder adder_4 (.A(A[3]), .B(B[3]), .Cin(adder_3_cout), .S(S[3]), .Cout(adder_4_cout));
  adder adder_5 (.A(A[4]), .B(B[4]), .Cin(adder_4_cout), .S(S[4]), .Cout(adder_5_cout));
  adder adder_6 (.A(A[5]), .B(B[5]), .Cin(adder_5_cout), .S(S[5]), .Cout(adder_6_cout));
  adder adder_7 (.A(A[6]), .B(B[6]), .Cin(adder_6_cout), .S(S[6]), .Cout(adder_7_cout));
  adder adder_8 (.A(A[7]), .B(B[7]), .Cin(adder_7_cout), .S(S[7]), .Cout(adder_8_cout));
  adder adder_9 (.A(A[8]), .B(B[8]), .Cin(adder_8_cout), .S(S[8]), .Cout(adder_9_cout));
  adder adder_10 (.A(A[9]), .B(B[9]), .Cin(adder_9_cout), .S(S[9]), .Cout(adder_10_cout));
  adder adder_11 (.A(A[10]), .B(B[10]), .Cin(adder_10_cout), .S(S[10]), .Cout(adder_11_cout));
  adder adder_12 (.A(A[11]), .B(B[11]), .Cin(adder_11_cout), .S(S[11]), .Cout(adder_12_cout));
  adder adder_13 (.A(A[12]), .B(B[12]), .Cin(adder_12_cout), .S(S[12]), .Cout(adder_13_cout));
  adder adder_14 (.A(A[13]), .B(B[13]), .Cin(adder_13_cout), .S(S[13]), .Cout(adder_14_cout));
  adder adder_15 (.A(A[14]), .B(B[14]), .Cin(adder_14_cout), .S(S[14]), .Cout(adder_15_cout));
  adder adder_16 (.A(A[15]), .B(B[15]), .Cin(adder_15_cout), .S(S[15]), .Cout(Cout));
endmodule

module alu2 (
  input  [15:0] A,
  input  [15:0] B,
  input  [3:0] OP,
  output EQ,
  output LT,
  output [15:0] RESULT,
  output [15:0] HI
);

  wire [15:0] adder_1_out, and_1_out, divider_1_out, divider_1_rem, multiplier_1_cout, multiplier_1_out,
       nor_1_out, or_1_out, shifter_1_out, shifter_2_out, shifter_3_out, subtractor_1_out, xor_1_out;

  Comparator #(.width(16)) comparator_1 (.a(A), .b(B), .eq(EQ), .lt(LT));  // open: gt
  Adder #(.width(16)) adder_1 (.a(A), .b(B), .out(adder_1_out));  // open: cin, cout
  Subtractor #(.width(16)) subtractor_1 (.a(A), .b(B), .out(subtractor_1_out));  // open: bin, bout
  Shifter #(.width(16)) shifter_1 (.in(A), .\dist (B[3:0]), .out(shifter_1_out));
  Shifter #(.width(16), .shift("lr")) shifter_2 (.in(A), .\dist (B[3:0]), .out(shifter_2_out));
  Shifter #(.width(16), .shift("ar")) shifter_3 (.in(A), .\dist (B[3:0]), .out(shifter_3_out));
  assign and_1_out = A & B;  // AND_Gate and_1, 16 bits wide
  assign or_1_out = A | B;  // OR_Gate or_1, 16 bits wide
  assign nor_1_out = ~(A | B);  // NOR_Gate nor_1, 16 bits wide
  assign xor_1_out = A ^ B;  // XOR_Gate xor_1, 16 bits wide
  Multiplier #(.width(16)) multiplier_1 (.a(A), .b(B), .out(multiplier_1_out), .cout(multiplier_1_cout));  // open: cin
  Divider #(.width(16)) divider_1 (.a(A), .b(B), .out(divider_1_out), .rem(divider_1_rem));  // open: upper
  Multiplexer #(.select(4), .width(16)) multiplexer_1 (
    .in0(adder_1_out), .in1(subtractor_1_out), .in2(shifter_1_out), .in3(shifter_2_out), .in4(shifter_3_out),
    .in5(and_1_out), .in6(or_1_out), .in7(nor_1_out), .in8(xor_1_out), .in9(multiplier_1_out),
    .in10(divider_1_out), .out(RESULT), .sel(OP));  // open: in11, in12, in13, in14, in15
  Multiplexer #(.select(4), .width(16)) multiplexer_2 (
    .in9(multiplier_1_cout), .in10(divider_1_rem), .out(HI), .sel(OP));  // open: in0, in1, in2, in3, in4, in5, in6, in7, in8, in11, in12, in13, in14, in15
  Pull_Resistor pull_resistor_1 (.node(RESULT));
  Pull_Resistor pull_resistor_2 (.node(HI));
endmodule

module cpu2 (
  input  IR_WRT,
  input  OP_WRT,
  input  PC_SRC,
  input  PC_WRT,
  input  MDR_WRT,
  input  MAR_SRC,
  input  MAR_WRT,
  input  MEM_WRT
);

  wire CLOCK_out, decoder_1_out0, decoder_1_out1, decoder_1_out2, decoder_1_out3, decoder_1_out4,
       decoder_1_out5, decoder_1_out6, decoder_1_out7, nor_1_out, not_1_out, not_2_out, not_3_out, or_1_out,
       or_2_out, or_3_out;
  wire [2:0] counter_1_q;
  wire [15:0] adder_1_out, IR_q, MAR_q, MDR_q, multiplexer_1_out, multiplexer_2_out, OP_q, PC_q, ram_1_data;

  Clock CLOCK (.out(CLOCK_out));
  Adder #(.width(16)) adder_1 (.a(PC_q), .b(16'h1), .out(adder_1_out));  // open: cin, cout
  Multiplexer #(.width(16)) multiplexer_1 (.in0(adder_1_out), .out(multiplexer_1_out), .sel(not_1_out));  // open: in1
  not not_1 (not_1_out, or_1_out);
  not not_2 (not_2_out, CLOCK_out);
  Counter #(.width(3), .max('h7)) counter_1 (.Q(counter_1_q), .clk(CLOCK_out));  // open: load, D, count, carry, clr
  Register #(.width(16)) PC (.D(multiplexer_1_out), .en(or_1_out), .Q(PC_q), .clk(not_2_out));  // open: clr
  Decoder #(.select(3)) decoder_1 (
    .out0(decoder_1_out0), .out1(decoder_1_out1), .out2(decoder_1_out2), .out3(decoder_1_out3),
    .out4(decoder_1_out4), .out5(decoder_1_out5), .out6(decoder_1_out6), .out7(decoder_1_out7),
    .sel(counter_1_q));
  or or_1 (or_1_out, decoder_1_out1, decoder_1_out3);
  Register #(.width(16)) IR (.D(MDR_q), .en(decoder_1_out2), .Q(IR_q), .clk(not_2_out));  // open: clr
  Multiplexer #(.width(16)) multiplexer_2 (.in0(PC_q), .out(multiplexer_2_out), .sel(nor_1_out));  // open: in1
  nor nor_1 (nor_1_out, decoder_1_out0, decoder_1_out2);
  or or_2 (or_2_out, decoder_1_out0, decoder_1_out2);
  Register #(.width(16)) MAR (.D(multiplexer_2_out), .en(or_2_out), .Q(MAR_q), .clk(not_2_out));  // open: clr
  Register #(.width(16)) OP (.D(MDR_q), .en(decoder_1_out4), .Q(OP_q), .clk(not_2_out));  // open: clr
  not not_3 (not_3_out, MEM_WRT);
  RAM #(.addrWidth(16), .dataWidth(16), .bus("separate")) ram_1 (
    .addr(MAR_q), .data(ram_1_data), .str(MEM_WRT), .clk(not_2_out), .ld(not_3_out));  // open: din, sel, clr
  or or_3 (or_3_out, decoder_1_out1, decoder_1_out3);
  Register #(.width(16)) MDR (.D(ram_1_data), .en(or_3_out), .Q(MDR_q), .clk(not_2_out));  // open: clr
endmodule

module cpu2a (
  input  CLOCK_IN,
  input  RESET,
  input  [15:0] DATA_IN,
  output MEM_WRT,
  output [15:0] DATA_OUT,
  output [15:0] ADDRESS,
  output HALT
);

  wire alu2_1_eq, alu2_1_lt, control_1_alu_b_src, control_1_fetch_2, control_1_hi_wrt, control_1_ir_wrt,
       control_1_lo_wrt, control_1_mar_src, control_1_op_wrt, control_1_reg_src2_src, control_1_reg_write,
       control_1_result_wrt, control_1_t_reset, controlled_buffer_1_out, d_ff_1_q, FETCH_q,
       multiplexer_2_out, not_1_out, not_2_out, not_3_out, or_1_out;
  wire [1:0] control_1_pc_src, control_1_pc_wrt;
  wire [2:0] control_1_reg_src;
  wire [3:0] control_1_alu_op, IR_q, IR_q_2, multiplexer_6_out, T_q;
  wire [7:0] IR_q_3;
  wire [11:0] OP_q;
  wire [15:0] adder_1_out, adder_2_out, alu2_1_hi, alu2_1_result, bit_extender_1_out, HI_q, LO_q,
       multiplexer_1_out, multiplexer_4_out, multiplexer_5_out, PC_q, reg2a_1_src1_out, RESULT_q,
       shifter_1_out;
  wire [15:12] OP_q_2;

  Shifter #(.width(16)) shifter_1 (.in({OP_q_2, OP_q}), .\dist (4'b0001), .out(shifter_1_out));
  not not_1 (not_1_out, alu2_1_eq);
  assign controlled_buffer_1_out = not_2_out ? CLOCK_IN : 1'bz;  // Controlled_Buffer controlled_buffer_1
  not not_2 (not_2_out, HALT);
  Adder #(.width(16)) adder_1 (.a(PC_q), .b(shifter_1_out), .out(adder_1_out));  // open: cin, cout
  Adder #(.width(16)) adder_2 (.a(PC_q), .b(16'h1), .out(adder_2_out));  // open: cin, cout
  not not_3 (not_3_out, controlled_buffer_1_out);
  // Probe on adder_1_out
  Multiplexer #(.select(2), .width(16)) multiplexer_1 (
    .in0(adder_2_out), .in1(adder_1_out), .in2({OP_q_2, OP_q}), .in3(DATA_OUT), .out(multiplexer_1_out),
    .sel(control_1_pc_src));
  Counter #(.width(4), .max('hf)) T (.Q(T_q), .clk(not_3_out), .clr(or_1_out));  // open: load, D, count, carry
  Register #(.width(16)) PC (
    .D(multiplexer_1_out), .en(multiplexer_2_out), .Q(PC_q), .clk(controlled_buffer_1_out), .clr(RESET));
  Multiplexer #(.select(2)) multiplexer_2 (
    .in0(1'b0), .in1(1'b1), .in2(alu2_1_eq), .in3(not_1_out), .out(multiplexer_2_out), .sel(control_1_pc_wrt));
  D_Flip_Flop FETCH (.clk(not_3_out), .D(control_1_fetch_2), .Q(FETCH_q), .preset(RESET));  // open: Qn, en, reset
  or or_1 (or_1_out, d_ff_1_q, RESET);
  D_Flip_Flop d_ff_1 (.clk(not_3_out), .D(control_1_t_reset), .Q(d_ff_1_q));  // open: Qn, preset, en, reset
  control control_1 (
    .INSTRUCTION(IR_q_3[4:0]), .FETCH(FETCH_q), .T(T_q), .HALT(HALT), .T_RESET(control_1_t_reset),
    .FETCH_2(control_1_fetch_2), .PC_SRC(control_1_pc_src), .PC_WRT(control_1_pc_wrt),
    .MAR_SRC(control_1_mar_src), .MEM_WRT(MEM_WRT), .IR_WRT(control_1_ir_wrt), .OP_WRT(control_1_op_wrt),
    .REG_SRC(control_1_reg_src), .REG_WRITE(control_1_reg_write), .ALU_B_SRC(control_1_alu_b_src),
    .REG_SRC2_SRC(control_1_reg_src2_src), .ALU_OP(control_1_alu_op), .RESULT_WRT(control_1_result_wrt),
    .LO_WRT(control_1_lo_wrt), .HI_WRT(control_1_hi_wrt));
  Register #(.width(16)) IR (
    .D(DATA_IN), .en(control_1_ir_wrt), .Q({IR_q_3, IR_q_2, IR_q}), .clk(controlled_buffer_1_out));  // open: clr
  Multiplexer #(.width(16)) multiplexer_3 (.in0(PC_q), .in1(RESULT_q), .out(ADDRESS), .sel(control_1_mar_src));
  // Probe on DATA_IN
  Multiplexer #(.select(3), .width(16)) multiplexer_4 (
    .in0(RESULT_q), .in1(bit_extender_1_out), .in2(PC_q), .in3(HI_q), .in4(LO_q), .in5(DATA_IN),
    .out(multiplexer_4_out), .sel(control_1_reg_src));  // open: in6, in7
  Register #(.width(16)) OP (
    .D(DATA_IN), .en(control_1_op_wrt), .Q({OP_q_2, OP_q}), .clk(controlled_buffer_1_out));  // open: clr
  reg2a reg2a_1 (
    .SRC1_REG(IR_q), .SRC2_REG(multiplexer_6_out), .CLOCK(controlled_buffer_1_out),
    .WRITE(control_1_reg_write), .DATA_IN(multiplexer_4_out), .DST_REG(IR_q_2), .SRC1_OUT(reg2a_1_src1_out),
    .SRC2_OUT(DATA_OUT));
  Multiplexer #(.width(16)) multiplexer_5 (
    .in0(DATA_OUT), .in1({OP_q_2, OP_q}), .out(multiplexer_5_out), .sel(control_1_alu_b_src));
  Multiplexer #(.width(4)) multiplexer_6 (
    .in0(OP_q_2), .in1(IR_q_2), .out(multiplexer_6_out), .sel(control_1_reg_src2_src));
  alu2 alu2_1 (
    .A(reg2a_1_src1_out), .B(multiplexer_5_out), .OP(control_1_alu_op), .EQ(alu2_1_eq), .LT(alu2_1_lt),
    .RESULT(alu2_1_result), .HI(alu2_1_hi));
  Register #(.width(16)) LO (
    .D(alu2_1_result), .en(control_1_lo_wrt), .Q(LO_q), .clk(controlled_buffer_1_out));  // open: clr
  assign bit_extender_1_out = {{15{1'b0}}, alu2_1_lt};  // Bit_Extender bit_extender_1
  Register #(.width(16)) HI (
    .D(alu2_1_hi), .en(control_1_hi_wrt), .Q(HI_q), .clk(controlled_buffer_1_out));  // open: clr
  Register #(.width(16)) RESULT (
    .D(alu2_1_result), .en(control_1_result_wrt), .Q(RESULT_q), .clk(controlled_buffer_1_out));  // open: clr
endmodule

module reg2a (
  input  [3:0] SRC1_REG,
  input  [3:0] SRC2_REG,
  input  CLOCK,
  input  WRITE,
  input  [15:0] DATA_IN,
  input  [3:0] DST_REG,
  output [15:0] SRC1_OUT,
  output [15:0] SRC2_OUT
);

  wire and_1_out, and_2_out, and_3_out, and_4_out, and_5_out, and_6_out, and_7_out, and_8_out, and_9_out,
       and_10_out, and_11_out, and_12_out, and_13_out, and_14_out, and_15_out, decoder_1_out1,
       decoder_1_out2, decoder_1_out3, decoder_1_out4, decoder_1_out5, decoder_1_out6, decoder_1_out7,
       decoder_1_out8, decoder_1_out9, decoder_1_out10, decoder_1_out11, decoder_1_out12, decoder_1_out13,
       decoder_1_out14, decoder_1_out15, decoder_2_out0, decoder_2_out1, decoder_2_out2, decoder_2_out3,
       decoder_2_out4, decoder_2_out5, decoder_2_out6, decoder_2_out7, decoder_2_out8, decoder_2_out9,
       decoder_2_out10, decoder_2_out11, decoder_2_out12, decoder_2_out13, decoder_2_out14, decoder_2_out15,
       decoder_3_out0, decoder_3_out1, decoder_3_out2, decoder_3_out3, decoder_3_out4, decoder_3_out5,
       decoder_3_out6, decoder_3_out7, decoder_3_out8, decoder_3_out9, decoder_3_out10, decoder_3_out11,
       decoder_3_out12, decoder_3_out13, decoder_3_out14, decoder_3_out15;
  wire [15:0] R1_q, R2_q, R3_q, R4_q, R5_q, R6_q, R7_q, R8_q, R9_q, R10_q, R11_q, R12_q, R13_q, R14_q, R15_q;

  Decoder #(.select(4)) decoder_1 (
    .out1(decoder_1_out1), .out2(decoder_1_out2), .out3(decoder_1_out3), .out4(decoder_1_out4),
    .out5(decoder_1_out5), .out6(decoder_1_out6), .out7(decoder_1_out7), .out8(decoder_1_out8),
    .out9(decoder_1_out9), .out10(decoder_1_out10), .out11(decoder_1_out11), .out12(decoder_1_out12),
    .out13(decoder_1_out13), .out14(decoder_1_out14), .out15(decoder_1_out15), .sel(DST_REG));  // open: out0
  and and_1 (and_1_out, decoder_1_out1, WRITE);
  and and_2 (and_2_out, decoder_1_out2, WRITE);
  and and_3 (and_3_out, decoder_1_out3, WRITE);
  and and_4 (and_4_out, decoder_1_out4, WRITE);
  and and_5 (and_5_out, decoder_1_out5, WRITE);
  and and_6 (and_6_out, decoder_1_out6, WRITE);
  and and_7 (and_7_out, decoder_1_out7, WRITE);
  and and_8 (and_8_out, decoder_1_out8, WRITE);
  and and_9 (and_9_out, decoder_1_out9, WRITE);
  and and_10 (and_10_out, decoder_1_out10, WRITE);
  and and_11 (and_11_out, decoder_1_out11, WRITE);
  and and_12 (and_12_out, decoder_1_out12, WRITE);
  and and_13 (and_13_out, decoder_1_out13, WRITE);
  and and_14 (and_14_out, decoder_1_out14, WRITE);
  and and_15 (and_15_out, decoder_1_out15, WRITE);
  Register #(.width(16)) R1 (.D(DATA_IN), .en(and_1_out), .Q(R1_q), .clk(CLOCK));  // open: clr
  Register #(.width(16)) R2 (.D(DATA_IN), .en(and_2_out), .Q(R2_q), .clk(CLOCK));  // open: clr
  Register #(.width(16)) R3 (.D(DATA_IN), .en(and_3_out), .Q(R3_q), .clk(CLOCK));  // open: clr
  Register #(.width(16)) R4 (.D(DATA_IN), .en(and_4_out), .Q(R4_q), .clk(CLOCK));  // open: clr
  Register #(.width(16)) R5 (.D(DATA_IN), .en(and_5_out), .Q(R5_q), .clk(CLOCK));  // open: clr
  Register #(.width(16)) R6 (.D(DATA_IN), .en(and_6_out), .Q(R6_q), .clk(CLOCK));  // open: clr
  Register #(.width(16)) R7 (.D(DATA_IN), .en(and_7_out), .Q(R7_q), .clk(CLOCK));  // open: clr
  Register #(.width(16)) R8 (.D(DATA_IN), .en(and_8_out), .Q(R8_q), .clk(CLOCK));  // open: clr
  Register #(.width(16)) R9 (.D(DATA_IN), .en(and_9_out), .Q(R9_q), .clk(CLOCK));  // open: clr
  Register #(.width(16)) R10 (.D(DATA_IN), .en(and_10_out), .Q(R10_q), .clk(CLOCK));  // open: clr
  Register #(.width(16)) R11 (.D(DATA_IN), .en(and_11_out), .Q(R11_q), .clk(CLOCK));  // open: clr
  Register #(.width(16)) R12 (.D(DATA_IN), .en(and_12_out), .Q(R12_q), .clk(CLOCK));  // open: clr
  Register #(.width(16)) R13 (.D(DATA_IN), .en(and_13_out), .Q(R13_q), .clk(CLOCK));  // open: clr
  Register #(.width(16)) R14 (.D(DATA_IN), .en(and_14_out), .Q(R14_q), .clk(CLOCK));  // open: clr
  Register #(.width(16)) R15 (.D(DATA_IN), .en(and_15_out), .Q(R15_q), .clk(CLOCK));  // open: clr
  Decoder #(.select(4)) decoder_2 (
    .out0(decoder_2_out0), .out1(decoder_2_out1), .out2(decoder_2_out2), .out3(decoder_2_out3),
    .out4(decoder_2_out4), .out5(decoder_2_out5), .out6(decoder_2_out6), .out7(decoder_2_out7),
    .out8(decoder_2_out8), .out9(decoder_2_out9), .out10(decoder_2_out10), .out11(decoder_2_out11),
    .out12(decoder_2_out12), .out13(decoder_2_out13), .out14(decoder_2_out14), .out15(decoder_2_out15),
    .sel(SRC1_REG));
  assign SRC1_OUT = decoder_2_out0 ? {16{1'b0}} : 16'bz;  // Controlled_Buffer controlled_buffer_1
  assign SRC1_OUT = decoder_2_out1 ? R1_q : 16'bz;  // Controlled_Buffer controlled_buffer_2
  assign SRC1_OUT = decoder_2_out2 ? R2_q : 16'bz;  // Controlled_Buffer controlled_buffer_3
  assign SRC1_OUT = decoder_2_out3 ? R3_q : 16'bz;  // Controlled_Buffer controlled_buffer_4
  assign SRC1_OUT = decoder_2_out4 ? R4_q : 16'bz;  // Controlled_Buffer controlled_buffer_5
  assign SRC1_OUT = decoder_2_out5 ? R5_q : 16'bz;  // Controlled_Buffer controlled_buffer_6
  assign SRC1_OUT = decoder_2_out6 ? R6_q : 16'bz;  // Controlled_Buffer controlled_buffer_7
  assign SRC1_OUT = decoder_2_out7 ? R7_q : 16'bz;  // Controlled_Buffer controlled_buffer_8
  assign SRC1_OUT = decoder_2_out8 ? R8_q : 16'bz;  // Controlled_Buffer controlled_buffer_9
  assign SRC1_OUT = decoder_2_out9 ? R9_q : 16'bz;  // Controlled_Buffer controlled_buffer_10
  assign SRC1_OUT = decoder_2_out10 ? R10_q : 16'bz;  // Controlled_Buffer controlled_buffer_11
  assign SRC1_OUT = decoder_2_out11 ? R11_q : 16'bz;  // Controlled_Buffer controlled_buffer_12
  assign SRC1_OUT = decoder_2_out12 ? R12_q : 16'bz;  // Controlled_Buffer controlled_buffer_13
  assign SRC1_OUT = decoder_2_out13 ? R13_q : 16'bz;  // Controlled_Buffer controlled_buffer_14
  assign SRC1_OUT = decoder_2_out14 ? R14_q : 16'bz;  // Controlled_Buffer controlled_buffer_15
  assign SRC1_OUT = decoder_2_out15 ? R15_q : 16'bz;  // Controlled_Buffer controlled_buffer_16
  Decoder #(.select(4)) decoder_3 (
    .out0(decoder_3_out0), .out1(decoder_3_out1), .out2(decoder_3_out2), .out3(decoder_3_out3),
    .out4(decoder_3_out4), .out5(decoder_3_out5), .out6(decoder_3_out6), .out7(decoder_3_out7),
    .out8(decoder_3_out8), .out9(decoder_3_out9), .out10(decoder_3_out10), .out11(decoder_3_out11),
    .out12(decoder_3_out12), .out13(decoder_3_out13), .out14(decoder_3_out14), .out15(decoder_3_out15),
    .sel(SRC2_REG));
  assign SRC2_OUT = decoder_3_out0 ? {16{1'b0}} : 16'bz;  // Controlled_Buffer controlled_buffer_17
  assign SRC2_OUT = decoder_3_out1 ? R1_q : 16'bz;  // Controlled_Buffer controlled_buffer_18
  assign SRC2_OUT = decoder_3_out2 ? R2_q : 16'bz;  // Controlled_Buffer controlled_buffer_19
  assign SRC2_OUT = decoder_3_out3 ? R3_q : 16'bz;  // Controlled_Buffer controlled_buffer_20
  assign SRC2_OUT = decoder_3_out4 ? R4_q : 16'bz;  // Controlled_Buffer controlled_buffer_21
  assign SRC2_OUT = decoder_3_out5 ? R5_q : 16'bz;  // Controlled_Buffer controlled_buffer_22
  assign SRC2_OUT = decoder_3_out6 ? R6_q : 16'bz;  // Controlled_Buffer controlled_buffer_23
  assign SRC2_OUT = decoder_3_out7 ? R7_q : 16'bz;  // Controlled_Buffer controlled_buffer_24
  assign SRC2_OUT = decoder_3_out8 ? R8_q : 16'bz;  // Controlled_Buffer controlled_buffer_25
  assign SRC2_OUT = decoder_3_out9 ? R9_q : 16'bz;  // Controlled_Buffer controlled_buffer_26
  assign SRC2_OUT = decoder_3_out10 ? R10_q : 16'bz;  // Controlled_Buffer controlled_buffer_27
  assign SRC2_OUT = decoder_3_out11 ? R11_q : 16'bz;  // Controlled_Buffer controlled_buffer_28
  assign SRC2_OUT = decoder_3_out12 ? R12_q : 16'bz;  // Controlled_Buffer controlled_buffer_29
  assign SRC2_OUT = decoder_3_out13 ? R13_q : 16'bz;  // Controlled_Buffer controlled_buffer_30
  assign SRC2_OUT = decoder_3_out14 ? R14_q : 16'bz;  // Controlled_Buffer controlled_buffer_31
  assign SRC2_OUT = decoder_3_out15 ? R15_q : 16'bz;  // Controlled_Buffer controlled_buffer_32

  // Notes on the sheet:
  //   R0 ZERO
endmodule

module control (
  input  [4:0] INSTRUCTION,
  input  FETCH,
  input  [3:0] T,
  output HALT,
  output T_RESET,
  output FETCH_2,
  output [1:0] PC_SRC,
  output [1:0] PC_WRT,
  output MAR_SRC,
  output MEM_WRT,
  output IR_WRT,
  output OP_WRT,
  output [2:0] REG_SRC,
  output REG_WRITE,
  output ALU_B_SRC,
  output REG_SRC2_SRC,
  output [3:0] ALU_OP,
  output RESULT_WRT,
  output LO_WRT,
  output HI_WRT
);

  wire [4:0] multiplexer_1_out;

  Multiplexer #(.width(5)) multiplexer_1 (.in0(INSTRUCTION), .in1({5{1'b0}}), .out(multiplexer_1_out), .sel(FETCH));
  // Probe on {2'b00, FETCH, multiplexer_1_out, T}
  ROM #(.addrWidth(12), .dataWidth(24)) rom_1 (
    .addr({2'b00, FETCH, multiplexer_1_out, T}),
    .data({HALT, T_RESET, FETCH_2, PC_SRC, PC_WRT, MAR_SRC, MEM_WRT, IR_WRT, OP_WRT, REG_SRC, REG_WRITE, ALU_B_SRC, REG_SRC2_SRC, ALU_OP, RESULT_WRT, LO_WRT, HI_WRT}));  // open: sel

  // Notes on the sheet:
  //   contents of rom_1 (hex, n*v repeats v):
  //   4*800000 4 600200 14*800000 104 600200 14*800000 c 600200 14*800000 60004b 15*800000 600053
  //   15*800000 114 600200 14*800000 11c 600200 14*800000 124 600200 14*800000 14 600200 14*800000 1c
  //   600200 14*800000 24 600200 14*800000 6c0080 15*800000 6e0080 15*800000 600600 15*800000 600700
  //   15*800000 2c 600200 14*800000 12c 600200 14*800000 34 600200 14*800000 134 600200 14*800000 44
  //   600200 14*800000 3c 600200 14*800000 720000 15*800000 7a0000 15*800000 a00 720000 14*800000 a00
  //   7a0000 14*800000 104 611600 14*800000 104 618080 14*800000 600e00 15*800000 601200 59*800000 204000
  //   220000 202000 20000 3580*800000
endmodule

module total (
);

  wire and_1_out, CLOCK_out, comparator_1_eq, comparator_2_eq, comparator_3_eq, comparator_4_eq,
       comparator_5_eq, comparator_5_gt, comparator_6_eq, comparator_6_lt, comparator_7_eq, counter_2_carry,
       cpu2a_1_halt, cpu2a_1_mem_wrt, d_ff_1_q, not_1_out, not_2_out, not_3_out, not_4_out, or_1_out,
       or_2_out, or_3_out, RESET_out;
  wire [4:0] counter_3_q;
  wire [6:0] cpu2a_1_data_out;
  wire [8:0] cpu2a_1_data_out_2;
  wire [15:0] controlled_buffer_1_out, controlled_buffer_3_out, controlled_buffer_6_out,
       controlled_buffer_7_out, counter_1_q, counter_2_q, cpu2a_1_address, demultiplexer_1_out0,
       demultiplexer_1_out1, demultiplexer_1_out2, demultiplexer_1_out3, demultiplexer_1_out4,
       demultiplexer_1_out5, demultiplexer_1_out6, demultiplexer_1_out7, demultiplexer_1_out8,
       demultiplexer_1_out9, demultiplexer_1_out10, demultiplexer_1_out11, demultiplexer_1_out12,
       demultiplexer_1_out13, demultiplexer_1_out14, demultiplexer_1_out15, demultiplexer_1_out16,
       demultiplexer_1_out17, demultiplexer_1_out18, demultiplexer_1_out19, demultiplexer_1_out20,
       demultiplexer_1_out21, demultiplexer_1_out22, demultiplexer_1_out23, demultiplexer_1_out24,
       demultiplexer_1_out25, demultiplexer_1_out26, demultiplexer_1_out27, demultiplexer_1_out28,
       demultiplexer_1_out29, demultiplexer_1_out30, demultiplexer_1_out31, ram_1_data, ram_2_data,
       random_1_out;

  Clock CLOCK (.out(CLOCK_out));
  Button RESET (.out(RESET_out));
  D_Flip_Flop d_ff_1 (.clk(CLOCK_out), .D(counter_2_carry), .Q(d_ff_1_q));  // open: Qn, preset, en, reset
  cpu2a cpu2a_1 (
    .CLOCK_IN(CLOCK_out), .DATA_IN(controlled_buffer_1_out), .MEM_WRT(cpu2a_1_mem_wrt),
    .DATA_OUT({cpu2a_1_data_out_2, cpu2a_1_data_out}), .ADDRESS(cpu2a_1_address), .RESET(RESET_out),
    .HALT(cpu2a_1_halt));
  Counter #(.width(16), .max('hffff)) counter_1 (.Q(counter_1_q), .clk(d_ff_1_q));  // open: load, D, count, carry, clr
  LED HALT (.in(cpu2a_1_halt));
  Comparator #(.width(16), .mode("unsigned")) comparator_1 (
    .a(cpu2a_1_address), .b(16'hf002), .eq(comparator_1_eq));  // open: gt, lt
  Random #(.width(16)) random_1 (.clk(CLOCK_out), .out(random_1_out));  // open: next, clr
  Counter #(.width(16), .max('hffff)) counter_2 (
    .Q(counter_2_q), .carry(counter_2_carry), .clk(CLOCK_out));  // open: load, D, count, clr
  assign controlled_buffer_1_out = not_1_out ? controlled_buffer_3_out : 16'bz;  // Controlled_Buffer controlled_buffer_1
  assign controlled_buffer_1_out = comparator_1_eq ? random_1_out : 16'bz;  // Controlled_Buffer controlled_buffer_2
  not not_1 (not_1_out, comparator_1_eq);
  Comparator #(.width(16), .mode("unsigned")) comparator_2 (
    .a(cpu2a_1_address), .b(16'hfffe), .eq(comparator_2_eq));  // open: gt, lt
  Comparator #(.width(16), .mode("unsigned")) comparator_3 (
    .a(cpu2a_1_address), .b({16{1'b1}}), .eq(comparator_3_eq));  // open: gt, lt
  not not_2 (not_2_out, cpu2a_1_mem_wrt);
  RAM #(.addrWidth(16), .dataWidth(16), .bus("separate")) ram_1 (
    .addr(cpu2a_1_address), .din({cpu2a_1_data_out_2, cpu2a_1_data_out}), .data(ram_1_data),
    .str(cpu2a_1_mem_wrt), .clk(CLOCK_out), .ld(not_2_out));  // open: sel, clr
  assign controlled_buffer_3_out = comparator_7_eq ? counter_1_q : 16'bz;  // Controlled_Buffer controlled_buffer_3
  assign controlled_buffer_3_out = comparator_4_eq ? counter_2_q : 16'bz;  // Controlled_Buffer controlled_buffer_4
  Comparator #(.width(16), .mode("unsigned")) comparator_4 (
    .a(cpu2a_1_address), .b(16'hf000), .eq(comparator_4_eq));  // open: gt, lt
  or or_1 (or_1_out, comparator_4_eq, comparator_7_eq);
  not not_3 (not_3_out, or_1_out);
  assign controlled_buffer_3_out = not_3_out ? ram_1_data : 16'bz;  // Controlled_Buffer controlled_buffer_5
  Comparator #(.width(16), .mode("unsigned")) comparator_5 (
    .a(cpu2a_1_address), .b(16'ha000), .gt(comparator_5_gt), .eq(comparator_5_eq));  // open: lt
  Comparator #(.width(16), .mode("unsigned")) comparator_6 (
    .a(cpu2a_1_address), .b(16'ha01f), .eq(comparator_6_eq), .lt(comparator_6_lt));  // open: gt
  TTY tty_1 (.data(cpu2a_1_data_out), .clk(CLOCK_out), .we(comparator_2_eq), .clr(comparator_3_eq));
  Keyboard keyboard_1 ();  // open: clk, re, clr, avail, data
  Comparator #(.width(16), .mode("unsigned")) comparator_7 (
    .a(cpu2a_1_address), .b(16'hf001), .eq(comparator_7_eq));  // open: gt, lt
  or or_2 (or_2_out, comparator_5_gt, comparator_5_eq);
  or or_3 (or_3_out, comparator_6_eq, comparator_6_lt);
  assign controlled_buffer_6_out = and_1_out ? cpu2a_1_address : 16'bz;  // Controlled_Buffer controlled_buffer_6
  and and_1 (and_1_out, or_2_out, or_3_out);
  assign controlled_buffer_7_out = and_1_out ? {cpu2a_1_data_out_2, cpu2a_1_data_out} : 16'bz;  // Controlled_Buffer controlled_buffer_7
  Demultiplexer #(.select(5), .width(16)) demultiplexer_1 (
    .out0(demultiplexer_1_out0), .out1(demultiplexer_1_out1), .out2(demultiplexer_1_out2),
    .out3(demultiplexer_1_out3), .out4(demultiplexer_1_out4), .out5(demultiplexer_1_out5),
    .out6(demultiplexer_1_out6), .out7(demultiplexer_1_out7), .out8(demultiplexer_1_out8),
    .out9(demultiplexer_1_out9), .out10(demultiplexer_1_out10), .out11(demultiplexer_1_out11),
    .out12(demultiplexer_1_out12), .out13(demultiplexer_1_out13), .out14(demultiplexer_1_out14),
    .out15(demultiplexer_1_out15), .out16(demultiplexer_1_out16), .out17(demultiplexer_1_out17),
    .out18(demultiplexer_1_out18), .out19(demultiplexer_1_out19), .out20(demultiplexer_1_out20),
    .out21(demultiplexer_1_out21), .out22(demultiplexer_1_out22), .out23(demultiplexer_1_out23),
    .out24(demultiplexer_1_out24), .out25(demultiplexer_1_out25), .out26(demultiplexer_1_out26),
    .out27(demultiplexer_1_out27), .out28(demultiplexer_1_out28), .out29(demultiplexer_1_out29),
    .out30(demultiplexer_1_out30), .out31(demultiplexer_1_out31), .in(ram_2_data), .sel(counter_3_q));
  DotMatrix #(.inputtype("row"), .matrixcols(16), .matrixrows(32), .persist(64)) dotmatrix_1 (
    .row0(demultiplexer_1_out0), .row1(demultiplexer_1_out1), .row2(demultiplexer_1_out2),
    .row3(demultiplexer_1_out3), .row4(demultiplexer_1_out4), .row5(demultiplexer_1_out5),
    .row6(demultiplexer_1_out6), .row7(demultiplexer_1_out7), .row8(demultiplexer_1_out8),
    .row9(demultiplexer_1_out9), .row10(demultiplexer_1_out10), .row11(demultiplexer_1_out11),
    .row12(demultiplexer_1_out12), .row13(demultiplexer_1_out13), .row14(demultiplexer_1_out14),
    .row15(demultiplexer_1_out15), .row16(demultiplexer_1_out16), .row17(demultiplexer_1_out17),
    .row18(demultiplexer_1_out18), .row19(demultiplexer_1_out19), .row20(demultiplexer_1_out20),
    .row21(demultiplexer_1_out21), .row22(demultiplexer_1_out22), .row23(demultiplexer_1_out23),
    .row24(demultiplexer_1_out24), .row25(demultiplexer_1_out25), .row26(demultiplexer_1_out26),
    .row27(demultiplexer_1_out27), .row28(demultiplexer_1_out28), .row29(demultiplexer_1_out29),
    .row30(demultiplexer_1_out30), .row31(demultiplexer_1_out31));
  assign controlled_buffer_6_out[4:0] = not_4_out ? counter_3_q : 5'bz;  // Controlled_Buffer controlled_buffer_8
  not not_4 (not_4_out, and_1_out);
  Counter #(.width(5), .max('h1f)) counter_3 (.Q(counter_3_q), .clk(CLOCK_out));  // open: load, D, count, carry, clr
  RAM #(.addrWidth(5), .dataWidth(16), .bus("separate")) ram_2 (
    .addr(controlled_buffer_6_out[4:0]), .din(controlled_buffer_7_out), .data(ram_2_data), .str(and_1_out),
    .clk(CLOCK_out), .ld(not_4_out));  // open: sel, clr
endmodule

module control2 (
  input  [4:0] INSTRUCTION,
  input  FETCH,
  input  [3:0] T,
  output HALT,
  output T_RESET,
  output FETCH_2,
  output [1:0] PC_SRC,
  output [1:0] PC_WRT,
  output MAR_SRC,
  output MEM_WRT,
  output IR_WRT,
  output OP_WRT,
  output [2:0] REG_SRC,
  output REG_WRITE,
  output ALU_B_SRC,
  output REG_SRC2_SRC,
  output [3:0] ALU_OP,
  output RESULT_WRT,
  output LO_WRT,
  output HI_WRT
);

  wire and_2_out, and_4_out, and_5_out, and_6_out, and_7_out, and_9_out, and_10_out, and_12_out,
       decoder_1_out0, decoder_1_out1, decoder_1_out2, decoder_1_out11, decoder_1_out26, decoder_1_out31,
       decoder_2_out0, decoder_2_out1, decoder_2_out2, decoder_2_out3, decoder_2_out4, decoder_2_out5,
       not_1_out;

  not not_1 (not_1_out, FETCH);
  Decoder #(.select(5)) decoder_1 (
    .out0(decoder_1_out0), .out1(decoder_1_out1), .out2(decoder_1_out2), .out11(decoder_1_out11),
    .out26(decoder_1_out26), .out31(decoder_1_out31), .sel(INSTRUCTION));  // open: out3, out4, out5, out6, out7, out8, out9, out10, out12, out13, out14, out15, out16, out17, out18, out19, out20, out21, out22, out23, out24, out25, out27, out28, out29, out30
  Decoder #(.select(4)) decoder_2 (
    .out0(decoder_2_out0), .out1(decoder_2_out1), .out2(decoder_2_out2), .out3(decoder_2_out3),
    .out4(decoder_2_out4), .out5(decoder_2_out5), .sel(T));  // open: out6, out7, out8, out9, out10, out11, out12, out13, out14, out15
  and and_1 (IR_WRT, FETCH, decoder_2_out0);
  and and_2 (and_2_out, FETCH, decoder_2_out1);
  and and_3 (OP_WRT, FETCH, decoder_2_out2);
  and and_4 (and_4_out, FETCH, decoder_2_out3);
  and and_5 (and_5_out, decoder_1_out0, not_1_out, decoder_2_out4);
  and and_6 (and_6_out, decoder_1_out0, decoder_2_out5);
  and and_7 (and_7_out, decoder_1_out1, decoder_2_out4, not_1_out);
  and and_8 (HALT, decoder_1_out31, not_1_out);
  and and_9 (and_9_out, decoder_1_out1, decoder_2_out5);
  and and_10 (and_10_out, not_1_out, decoder_2_out4, decoder_1_out26);
  and and_11 (MAR_SRC, decoder_1_out26, decoder_2_out5);
  and and_12 (and_12_out, decoder_1_out11, decoder_2_out5, not_1_out);
  and and_13 (PC_SRC[0], decoder_1_out11, not_1_out);
  or or_1 (RESULT_WRT, and_5_out, and_7_out, and_10_out);
  or or_2 (PC_WRT[0], and_2_out, and_4_out);
  or or_3 (FETCH_2, MAR_SRC, IR_WRT, and_2_out, PC_SRC[0], OP_WRT, and_6_out, and_9_out);
  or or_4 (T_RESET, and_6_out, MAR_SRC, and_9_out, PC_SRC[0]);
  or or_5 (ALU_B_SRC, and_7_out, and_10_out);
  Pull_Resistor pull_resistor_1 (.node(ALU_OP[1]));
  Pull_Resistor pull_resistor_2 (.node(ALU_OP[3]));
  Pull_Resistor pull_resistor_3 (.node(ALU_OP[2]));
  Pull_Resistor pull_resistor_4 (.node(REG_SRC[0]));
  Pull_Resistor pull_resistor_5 (.node(REG_SRC[2]));
  Pull_Resistor pull_resistor_6 (.node(REG_SRC[1]));
  Pull_Resistor pull_resistor_7 (.node(ALU_OP[0]));
  Pull_Resistor pull_resistor_8 (.node(PC_WRT[0]));
  Pull_Resistor pull_resistor_9 (.node(PC_SRC[1]));
  Pull_Resistor pull_resistor_10 (.node(PC_SRC[0]));
  Pull_Resistor pull_resistor_11 (.node(PC_SRC[0]));
  or or_6 (REG_WRITE, and_6_out, and_9_out);
  or or_7 (REG_SRC2_SRC, MAR_SRC, and_12_out);
  Pull_Resistor pull_resistor_12 (.node(REG_SRC2_SRC));
  Pull_Resistor pull_resistor_13 (.node(LO_WRT));
  Pull_Resistor pull_resistor_14 (.node(HI_WRT));
  Pull_Resistor pull_resistor_15 (.node(RESULT_WRT));
  Pull_Resistor pull_resistor_16 (.node(ALU_B_SRC));
  Pull_Resistor pull_resistor_17 (.node(IR_WRT));
  Pull_Resistor pull_resistor_18 (.node(REG_WRITE));
  Pull_Resistor pull_resistor_19 (.node(OP_WRT));
  Pull_Resistor pull_resistor_20 (.node(MAR_SRC));
  Pull_Resistor pull_resistor_21 (.node(T_RESET));
  Pull_Resistor pull_resistor_22 (.node(FETCH_2));
  Pull_Resistor pull_resistor_23 (.node(MAR_SRC));
  Pull_Resistor pull_resistor_24 (.node(HALT));

  assign MEM_WRT = MAR_SRC;
  assign PC_WRT[1] = PC_SRC[0];
endmodule
