// Logisim project alu.circ as structural Verilog: 2 circuits, main circuit main
module main (
  input  [15:0] B,
  input  [15:0] A,
  input  u3,
  input  u2,
  input  u1,
  input  u0,
  output [15:0] out_7
);

  wire adder_1_cout, alu_control_1_nb, multiplexer_1_out, pull_resistor_1_node;
  wire [1:0] alu_control_1_cin0;
  wire [2:0] alu_control_1_res0;
  wire [15:0] adder_1_out, and_1_out, multiplexer_2_out, multiplier_1_cout, multiplier_1_out, not_1_out,
       not_2_out, or_1_out, xor_1_out;

  Pull_Resistor pull_resistor_1 (.node(pull_resistor_1_node));
  Multiplexer #(.select(2)) multiplexer_1 (
    .in0(pull_resistor_1_node), .in1(1'b1), .in3(adder_1_cout), .out(multiplexer_1_out),
    .sel(alu_control_1_cin0));  // open: in2
  // Probe on alu_control_1_cin0
  assign not_1_out = ~B;  // NOT_Gate not_1, 16 bits wide
  Multiplexer #(.width(16)) multiplexer_2 (.in0(B), .in1(not_1_out), .out(multiplexer_2_out), .sel(alu_control_1_nb));
  Adder #(.width(16)) adder_1 (
    .a(A), .b(multiplexer_2_out), .out(adder_1_out), .cin(multiplexer_1_out), .cout(adder_1_cout));
  assign not_2_out = ~A;  // NOT_Gate not_2, 16 bits wide
  Multiplier #(.width(16)) multiplier_1 (
    .a(A), .b(multiplexer_2_out), .out(multiplier_1_out), .cout(multiplier_1_cout));  // open: cin
  // Probe on alu_control_1_nb
  assign and_1_out = A & multiplexer_2_out;  // AND_Gate and_1, 16 bits wide
  assign or_1_out = A | multiplexer_2_out;  // OR_Gate or_1, 16 bits wide
  assign xor_1_out = A ^ multiplexer_2_out;  // XOR_Gate xor_1, 16 bits wide
  // Probe on multiplier_1_out
  // Probe on multiplier_1_cout
  Multiplexer #(.select(3), .width(16)) multiplexer_3 (
    .in0(adder_1_out), .in1(and_1_out), .in2(or_1_out), .in3(xor_1_out), .in4(not_2_out), .out(out_7),
    .sel(alu_control_1_res0));  // open: in5, in6, in7
  // Probe on alu_control_1_res0
  alu_control alu_control_1 (
    .u3(u3), .u2(u2), .u1(u1), .u0(u0), .res2(alu_control_1_res0[2]), .res1(alu_control_1_res0[1]),
    .res0(alu_control_1_res0[0]), .cin1(alu_control_1_cin0[1]), .cin0(alu_control_1_cin0[0]),
    .nb(alu_control_1_nb));
endmodule

module alu_control (
  input  u3,
  input  u2,
  input  u1,
  input  u0,
  output res2,
  output res1,
  output res0,
  output cin1,
  output cin0,
  output nb
);

  wire and_1_out, and_2_out, and_3_out, and_4_out, and_5_out, and_6_out, and_7_out, and_8_out, and_9_out,
       and_10_out, and_12_out, and_13_out, and_14_out, and_15_out, not_1_out, not_2_out, not_3_out,
       not_4_out, not_5_out, not_6_out, not_7_out, not_8_out, not_9_out, not_10_out, not_11_out, not_12_out,
       not_13_out, not_14_out;

  and and_1 (and_1_out, u2, not_1_out, u0);
  not not_1 (not_1_out, u1);
  and and_2 (and_2_out, u2, u1, not_2_out);
  not not_2 (not_2_out, u0);
  and and_3 (and_3_out, u3, u0);
  and and_4 (and_4_out, u3, u1);
  not not_3 (not_3_out, u2);
  and and_5 (and_5_out, not_3_out, u1, u0);
  and and_6 (and_6_out, u2, not_4_out, not_5_out);
  not not_4 (not_4_out, u1);
  not not_5 (not_5_out, u0);
  and and_7 (and_7_out, u3, u0);
  and and_8 (and_8_out, u3, u1);
  and and_9 (and_9_out, u1, not_6_out);
  not not_6 (not_6_out, u0);
  and and_10 (and_10_out, u2, not_7_out);
  not not_7 (not_7_out, u0);
  and and_11 (cin1, u2, u1, u0);
  and and_12 (and_12_out, u2, u1, u0);
  not not_8 (not_8_out, u1);
  and and_13 (and_13_out, u3, not_8_out, not_9_out);
  not not_9 (not_9_out, u0);
  not not_10 (not_10_out, u3);
  not not_11 (not_11_out, u2);
  not not_12 (not_12_out, u1);
  not not_13 (not_13_out, u1);
  not not_14 (not_14_out, u0);
  or or_1 (res2, and_1_out, and_2_out, and_3_out, and_4_out);
  or or_2 (res1, and_5_out, and_6_out, and_7_out, and_8_out);
  or or_3 (res0, and_9_out, and_10_out);
  or or_4 (cin0, and_12_out, and_13_out);
  and and_14 (and_14_out, not_10_out, not_11_out, not_12_out, u0);
  or or_5 (nb, and_14_out, and_15_out);
  and and_15 (and_15_out, u3, not_13_out, not_14_out);
endmodule
