// Logisim project alu2.circ as structural Verilog: 12 circuits, main circuit main
module main (
  input  [15:0] in_1,
  input  [15:0] in_2,
  input  [3:0] in_3,
  input  in_4,
  input  reg_write,
  input  b_src,
  input  [1:0] reg_sel,
  input  reg_src_dst,
  input  [1:0] a_src,
  input  [3:0] in_10,
  input  pc_src,
  input  ir_write,
  input  PC_write,
  input  mem_write,
  input  ir_fetch,
  input  op_fetch
);

  wire alu_1_c_out, alu_1_n, alu_1_v, alu_1_z, clock_1_out, not_1_out, not_2_out, not_3_out, not_4_out,
       or_1_out;
  wire [1:0] multiplexer_4_out;
  wire [15:0] alu_1_result, alu_2_result, bit_extender_1_out, bit_extender_2_out, IR_q, multiplexer_1_out,
       multiplexer_2_out, multiplexer_3_out, OP_q, PC_q, ram_1_data, reg_1_out, reg_latch_q;

  Clock clock_1 (.out(clock_1_out));
  not not_1 (not_1_out, 1'b1);
  assign bit_extender_1_out = {{15{1'b0}}, not_1_out};  // Bit_Extender bit_extender_1
  assign bit_extender_2_out = {{15{1'b0}}, 1'b1};  // Bit_Extender bit_extender_2
  Multiplexer #(.width(16)) multiplexer_1 (.in0(alu_2_result), .out(multiplexer_1_out), .sel(not_2_out));  // open: in1
  not not_2 (not_2_out, or_1_out);
  Register #(.width(16)) PC (.D(multiplexer_1_out), .en(or_1_out), .Q(PC_q), .clk(clock_1_out));  // open: clr
  Multiplexer #(.width(16)) multiplexer_2 (
    .in0(bit_extender_1_out), .in1(bit_extender_2_out), .out(multiplexer_2_out), .sel(or_1_out));
  Multiplexer #(.select(2), .width(16)) multiplexer_3 (
    .in0(PC_q), .out(multiplexer_3_out), .sel(a_src));  // open: in1, in2, in3
  or or_1 (or_1_out, ir_fetch, op_fetch);
  alu alu_1 (
    .V(alu_1_v), .N(alu_1_n), .result(alu_1_result), .C_out(alu_1_c_out), .Z(alu_1_z), .A(in_1), .B(in_2),
    .C_in(in_4), .op(in_3));
  // Probe on alu_1_result
  alu alu_2 (
    .result(alu_2_result), .A(multiplexer_3_out), .B(multiplexer_2_out), .op(in_10));  // open: V, N, C_out, Z, C_in
  not not_3 (not_3_out, mem_write);
  RAM #(.addrWidth(16), .dataWidth(16), .bus("separate")) ram_1 (
    .addr(PC_q), .data(ram_1_data), .str(mem_write), .clk(clock_1_out), .ld(not_3_out));  // open: din, sel, clr
  // Probe on ram_1_data
  Multiplexer #(.width(2)) multiplexer_4 (
    .in0(IR_q[9:8]), .in1(IR_q[11:10]), .out(multiplexer_4_out), .sel(reg_src_dst));
  Register #(.width(16)) IR (.D(ram_1_data), .en(ir_fetch), .Q(IR_q), .clk(clock_1_out));  // open: clr
  \reg  reg_1 (.clock(clock_1_out), .in(reg_latch_q), .in_3(multiplexer_4_out), .write(reg_write), .out(reg_1_out));
  Register #(.width(16)) OP (.D(ram_1_data), .en(op_fetch), .Q(OP_q), .clk(clock_1_out));  // open: clr
  not not_4 (not_4_out, clock_1_out);
  // Probe on IR_q[4:0]
  Register #(.width(16)) reg_latch (.D(reg_1_out), .Q(reg_latch_q), .clk(not_4_out));  // open: en, clr
  // Probe on reg_1_out
  // Probe on IR_q[7:5]
  // Probe on IR_q[15:12]
  // Probe on reg_latch_q
  // Probe on IR_q[9:8]
  // Probe on IR_q[11:10]
endmodule

module oveflow (
  input  a,
  input  b,
  input  r,
  output v
);

  wire and_1_out, and_2_out, and_3_out, and_4_out, not_1_out, not_2_out, not_3_out;

  not not_1 (not_1_out, a);
  not not_2 (not_2_out, b);
  and and_1 (and_1_out, not_1_out, not_2_out);
  and and_2 (and_2_out, a, b);
  not not_3 (not_3_out, r);
  and and_3 (and_3_out, and_1_out, r);
  and and_4 (and_4_out, and_2_out, not_3_out);
  or or_1 (v, and_3_out, and_4_out);
endmodule

module alu (
  input  C_in,
  input  [15:0] A,
  input  [15:0] B,
  input  [3:0] op,
  output V,
  output N,
  output [15:0] result,
  output C_out,
  output Z
);

  wire adder_1_cout, subtractor_1_bout;
  wire [15:0] adder_1_out, and_1_out, divider_1_out, multiplier_1_out, negator_1_out, not_1_out, or_1_out,
       subtractor_1_out, xor_1_out;

  Multiplier #(.width(16)) multiplier_1 (.a(A), .b(B), .out(multiplier_1_out));  // open: cin, cout
  Adder #(.width(16)) adder_1 (.a(A), .b(B), .out(adder_1_out), .cin(C_in), .cout(adder_1_cout));
  Divider #(.width(16)) divider_1 (.a(A), .b(B), .out(divider_1_out));  // open: upper, rem
  assign and_1_out = A & B;  // AND_Gate and_1, 16 bits wide
  assign or_1_out = A | B;  // OR_Gate or_1, 16 bits wide
  assign xor_1_out = A ^ B;  // XOR_Gate xor_1, 16 bits wide
  Subtractor #(.width(16)) subtractor_1 (.a(A), .b(B), .out(subtractor_1_out), .bin(C_in), .bout(subtractor_1_bout));
  assign not_1_out = ~A;  // NOT_Gate not_1, 16 bits wide
  Negator #(.width(16)) negator_1 (.in(A), .out(negator_1_out));
  Comparator #(.width(16)) comparator_1 (.a(A), .b(B));  // open: gt, eq, lt
  Multiplexer #(.select(4), .width(16)) multiplexer_1 (
    .in0(adder_1_out), .in1(subtractor_1_out), .in2(multiplier_1_out), .in3(divider_1_out), .in4(and_1_out),
    .in5(or_1_out), .in6(not_1_out), .in7(xor_1_out), .in13(negator_1_out), .out({N, result[14:0]}), .sel(op));  // open: in8, in9, in10, in11, in12, in14, in15
  Multiplexer #(.select(4)) multiplexer_2 (
    .in0(adder_1_cout), .in1(subtractor_1_bout), .out(C_out), .sel(op));  // open: in2, in3, in4, in5, in6, in7, in8, in9, in10, in11, in12, in13, in14, in15
  oveflow oveflow_1 (.a(A[15]), .b(B[15]), .r(N), .v(V));
  Pull_Resistor pull_resistor_1 (.node(C_out));
  nor nor_1 (Z, result[0], result[1], result[2], result[3], result[4], result[5], result[6], result[7], result[8], result[9], result[10], result[11], result[12], result[13], result[14], N);

  assign result[15] = N;
endmodule

module \reg  (
  input  clock,
  input  [15:0] in,
  input  [1:0] in_3,
  input  write,
  output [15:0] out
);

  wire demultiplexer_1_out0, demultiplexer_1_out1, demultiplexer_1_out2, demultiplexer_1_out3;
  wire [15:0] A_q, B_q, X_q, Y_q;

  Register #(.width(16)) A (.D(in), .en(demultiplexer_1_out0), .Q(A_q), .clk(clock));  // open: clr
  Register #(.width(16)) X (.D(in), .en(demultiplexer_1_out2), .Q(X_q), .clk(clock));  // open: clr
  Demultiplexer #(.select(2)) demultiplexer_1 (
    .out0(demultiplexer_1_out0), .out1(demultiplexer_1_out1), .out2(demultiplexer_1_out2),
    .out3(demultiplexer_1_out3), .in(write), .sel(in_3));
  Register #(.width(16)) B (.D(in), .en(demultiplexer_1_out1), .Q(B_q), .clk(clock));  // open: clr
  Register #(.width(16)) Y (.D(in), .en(demultiplexer_1_out3), .Q(Y_q), .clk(clock));  // open: clr
  Multiplexer #(.select(2), .width(16)) multiplexer_1 (
    .in0(A_q), .in1(B_q), .in2(X_q), .in3(Y_q), .out(out), .sel(in_3));
endmodule

module reg2 (
  input  clock,
  input  [15:0] in,
  input  [1:0] in_3,
  input  write,
  input  [15:0] in_2,
  input  [2:0] in_6,
  input  in_7,
  output [15:0] out
);

  wire clock_1_out, demultiplexer_1_out0, demultiplexer_1_out1, demultiplexer_1_out2, demultiplexer_1_out3;
  wire [15:0] A_q, B_q, multiplexer_1_out, register_1_q, X_q, Y_q;

  Clock clock_1 (.out(clock_1_out));
  Demultiplexer #(.select(2)) demultiplexer_1 (
    .out0(demultiplexer_1_out0), .out1(demultiplexer_1_out1), .out2(demultiplexer_1_out2),
    .out3(demultiplexer_1_out3), .in(write), .sel(in_3));
  Register #(.width(16)) A (.D(in), .en(demultiplexer_1_out0), .Q(A_q), .clk(clock));  // open: clr
  Register #(.width(16)) X (.D(in), .en(demultiplexer_1_out2), .Q(X_q), .clk(clock));  // open: clr
  Register #(.width(16)) B (.D(in), .en(demultiplexer_1_out1), .Q(B_q), .clk(clock));  // open: clr
  Register #(.width(16)) Y (.D(in), .en(demultiplexer_1_out3), .Q(Y_q), .clk(clock));  // open: clr
  Multiplexer #(.select(3), .width(16)) multiplexer_1 (
    .in0(register_1_q), .in4(in_2), .out(multiplexer_1_out), .sel(in_6));  // open: in1, in2, in3, in5, in6, in7
  Multiplexer #(.select(2), .width(16)) multiplexer_2 (
    .in0(A_q), .in1(B_q), .in2(X_q), .in3(Y_q), .out(out), .sel(in_3));
  Register #(.width(16)) register_1 (
    .D(multiplexer_1_out), .en(in_7), .Q(register_1_q), .clk(clock_1_out));  // open: clr
endmodule

module clk2 (
);

  wire button_1_out, clock_1_out, d_ff_1_q, d_ff_1_qn, d_ff_2_q, d_ff_2_qn;
  wire [7:0] counter_1_q, counter_2_q, counter_3_q;

  Clock clock_1 (.out(clock_1_out));
  Counter counter_1 (.Q(counter_1_q), .clk(clock_1_out), .clr(button_1_out));  // open: load, D, count, carry
  Button button_1 (.out(button_1_out));
  LED led_1 (.in(clock_1_out));
  D_Flip_Flop d_ff_1 (.clk(clock_1_out), .D(d_ff_1_qn), .Q(d_ff_1_q), .Qn(d_ff_1_qn));  // open: preset, en, reset
  LED led_2 (.in(d_ff_1_q));
  LED led_3 (.in(d_ff_2_q));
  Counter counter_2 (.Q(counter_2_q), .clk(d_ff_1_q), .clr(button_1_out));  // open: load, D, count, carry
  D_Flip_Flop d_ff_2 (.clk(d_ff_1_q), .D(d_ff_2_qn), .Q(d_ff_2_q), .Qn(d_ff_2_qn));  // open: preset, en, reset
  Counter counter_3 (.Q(counter_3_q), .clk(d_ff_2_q), .clr(button_1_out));  // open: load, D, count, carry
  DotMatrix #(.matrixcols(3), .matrixrows(8)) dotmatrix_1 (.col0(counter_1_q), .col1(counter_2_q), .col2(counter_3_q));
endmodule

module bus (
  input  [1:0] in_1,
  input  [15:0] in_2,
  input  in_3,
  input  in_4,
  input  [15:0] in_5,
  input  in,
  input  in_7
);

  wire clock_1_out, decoder_1_out0, decoder_1_out1, decoder_1_out2, not_1_out;
  wire [15:0] controlled_buffer_1_out, controlled_buffer_2_out, controlled_buffer_3_out,
       controlled_buffer_4_out, register_1_q;

  Clock clock_1 (.out(clock_1_out));
  assign controlled_buffer_1_out = decoder_1_out0 ? in_2 : 16'bz;  // Controlled_Buffer controlled_buffer_1
  assign controlled_buffer_2_out = in ? in_5 : 16'bz;  // Controlled_Buffer controlled_buffer_2
  // Probe on controlled_buffer_1_out
  // Probe on controlled_buffer_2_out
  Decoder #(.select(2)) decoder_1 (
    .out0(decoder_1_out0), .out1(decoder_1_out1), .out2(decoder_1_out2), .sel(in_1));  // open: out3
  assign controlled_buffer_3_out = decoder_1_out2 ? controlled_buffer_1_out : 16'bz;  // Controlled_Buffer controlled_buffer_3
  not not_1 (not_1_out, in_7);
  Register #(.width(16)) register_1 (
    .D(controlled_buffer_3_out), .en(decoder_1_out2), .Q(register_1_q), .clk(clock_1_out));  // open: clr
  assign controlled_buffer_4_out = in_7 ? controlled_buffer_1_out : 16'bz;  // Controlled_Buffer controlled_buffer_4
  RAM #(.addrWidth(16), .dataWidth(16)) ram_1 (
    .addr(controlled_buffer_2_out), .data(controlled_buffer_4_out), .clk(clock_1_out), .ld(not_1_out));  // open: sel, clr
  assign controlled_buffer_1_out = decoder_1_out1 ? controlled_buffer_4_out : 16'bz;  // Controlled_Buffer controlled_buffer_5
endmodule

module bus2 (
  input  [2:0] addr_src,
  input  [2:0] data_src,
  input  [2:0] addr_dst,
  input  in_4,
  input  [2:0] data_dst
);

  wire and_1_out, clock_1_out, decoder_1_out0, decoder_1_out1, decoder_1_out2, decoder_1_out3,
       decoder_1_out4, decoder_1_out6, decoder_1_out7, decoder_2_out0, decoder_2_out1, decoder_2_out2,
       decoder_2_out3, decoder_2_out4, decoder_2_out6, decoder_2_out7, decoder_3_out0, decoder_3_out1,
       decoder_3_out2, decoder_3_out3, decoder_3_out5, decoder_3_out6, decoder_4_out4, decoder_4_out5,
       not_1_out;
  wire [15:0] A_q, B_q, bit_extender_1_out, controlled_buffer_1_out, controlled_buffer_2_out,
       controlled_buffer_3_out, controlled_buffer_5_out, controlled_buffer_7_out, controlled_buffer_9_out,
       controlled_buffer_11_out, controlled_buffer_14_out, controlled_buffer_18_out,
       controlled_buffer_20_out, controlled_buffer_22_out, D_q, IR_q, PC_q, X_q, Y_q;

  Clock clock_1 (.out(clock_1_out));
  Register #(.width(16)) D (.D(controlled_buffer_1_out), .en(decoder_2_out6), .Q(D_q), .clk(and_1_out));  // open: clr
  Decoder #(.select(3)) decoder_1 (
    .out0(decoder_1_out0), .out1(decoder_1_out1), .out2(decoder_1_out2), .out3(decoder_1_out3),
    .out4(decoder_1_out4), .out6(decoder_1_out6), .out7(decoder_1_out7), .sel(data_src));  // open: out5
  and and_1 (and_1_out, clock_1_out, in_4);
  Register #(.width(16)) IR (.D(controlled_buffer_3_out), .en(decoder_2_out7), .Q(IR_q), .clk(and_1_out));  // open: clr
  assign controlled_buffer_1_out = decoder_2_out6 ? controlled_buffer_2_out : 16'bz;  // Controlled_Buffer controlled_buffer_1
  assign controlled_buffer_2_out = decoder_1_out6 ? D_q : 16'bz;  // Controlled_Buffer controlled_buffer_2
  assign controlled_buffer_3_out = decoder_2_out7 ? controlled_buffer_2_out : 16'bz;  // Controlled_Buffer controlled_buffer_3
  assign controlled_buffer_2_out = decoder_1_out7 ? IR_q : 16'bz;  // Controlled_Buffer controlled_buffer_4
  Register #(.width(16)) Y (.D(controlled_buffer_5_out), .en(decoder_2_out3), .Q(Y_q), .clk(and_1_out));  // open: clr
  Register #(.width(16)) X (.D(controlled_buffer_7_out), .en(decoder_2_out2), .Q(X_q), .clk(and_1_out));  // open: clr
  Register #(.width(16)) B (.D(controlled_buffer_9_out), .en(decoder_2_out1), .Q(B_q), .clk(and_1_out));  // open: clr
  Register #(.width(16)) A (.D(controlled_buffer_11_out), .en(decoder_2_out0), .Q(A_q), .clk(and_1_out));  // open: clr
  Decoder #(.select(3)) decoder_2 (
    .out0(decoder_2_out0), .out1(decoder_2_out1), .out2(decoder_2_out2), .out3(decoder_2_out3),
    .out4(decoder_2_out4), .out6(decoder_2_out6), .out7(decoder_2_out7), .sel(data_dst));  // open: out5
  assign controlled_buffer_5_out = decoder_2_out3 ? controlled_buffer_2_out : 16'bz;  // Controlled_Buffer controlled_buffer_5
  assign controlled_buffer_2_out = decoder_1_out2 ? Y_q : 16'bz;  // Controlled_Buffer controlled_buffer_6
  assign controlled_buffer_7_out = decoder_2_out2 ? controlled_buffer_2_out : 16'bz;  // Controlled_Buffer controlled_buffer_7
  assign controlled_buffer_2_out = decoder_1_out3 ? X_q : 16'bz;  // Controlled_Buffer controlled_buffer_8
  assign controlled_buffer_9_out = decoder_2_out1 ? controlled_buffer_2_out : 16'bz;  // Controlled_Buffer controlled_buffer_9
  assign controlled_buffer_2_out = decoder_1_out1 ? B_q : 16'bz;  // Controlled_Buffer controlled_buffer_10
  assign controlled_buffer_11_out = decoder_2_out0 ? controlled_buffer_2_out : 16'bz;  // Controlled_Buffer controlled_buffer_11
  assign controlled_buffer_2_out = decoder_1_out0 ? A_q : 16'bz;  // Controlled_Buffer controlled_buffer_12
  // Probe on controlled_buffer_2_out
  assign controlled_buffer_2_out = decoder_1_out4 ? controlled_buffer_18_out : 16'bz;  // Controlled_Buffer controlled_buffer_13
  not not_1 (not_1_out, decoder_2_out4);
  assign controlled_buffer_14_out = decoder_3_out3 ? Y_q : 16'bz;  // Controlled_Buffer controlled_buffer_14
  assign controlled_buffer_14_out = decoder_3_out2 ? X_q : 16'bz;  // Controlled_Buffer controlled_buffer_15
  assign controlled_buffer_14_out = decoder_3_out1 ? B_q : 16'bz;  // Controlled_Buffer controlled_buffer_16
  assign controlled_buffer_14_out = decoder_3_out0 ? A_q : 16'bz;  // Controlled_Buffer controlled_buffer_17
  assign controlled_buffer_18_out = decoder_2_out4 ? controlled_buffer_2_out : 16'bz;  // Controlled_Buffer controlled_buffer_18
  assign controlled_buffer_14_out = decoder_3_out6 ? D_q : 16'bz;  // Controlled_Buffer controlled_buffer_19
  // Probe on controlled_buffer_14_out
  assign controlled_buffer_20_out = decoder_4_out5 ? controlled_buffer_14_out : 16'bz;  // Controlled_Buffer controlled_buffer_20
  assign bit_extender_1_out = {{15{1'b0}}, 1'b1};  // Bit_Extender bit_extender_1
  assign controlled_buffer_14_out = decoder_3_out5 ? PC_q : 16'bz;  // Controlled_Buffer controlled_buffer_21
  assign controlled_buffer_22_out = decoder_4_out4 ? controlled_buffer_14_out : 16'bz;  // Controlled_Buffer controlled_buffer_22
  Adder #(.width(16)) adder_1 (.a(PC_q), .b(bit_extender_1_out), .out(controlled_buffer_20_out));  // open: cin, cout
  Register #(.width(16)) PC (.D(controlled_buffer_20_out), .Q(PC_q), .clk(and_1_out));  // open: en, clr
  Decoder #(.select(3)) decoder_3 (
    .out0(decoder_3_out0), .out1(decoder_3_out1), .out2(decoder_3_out2), .out3(decoder_3_out3),
    .out5(decoder_3_out5), .out6(decoder_3_out6), .sel(addr_src));  // open: out4, out7
  Decoder #(.select(3)) decoder_4 (
    .out4(decoder_4_out4), .out5(decoder_4_out5), .sel(addr_dst));  // open: out0, out1, out2, out3, out6, out7
  // Probe on controlled_buffer_20_out
  RAM #(.addrWidth(16), .dataWidth(16)) ram_1 (
    .addr(controlled_buffer_22_out), .data(controlled_buffer_18_out), .clk(and_1_out), .ld(not_1_out));  // open: sel, clr
  // Probe on controlled_buffer_18_out
endmodule

module cpu (
  input  [1:0] in_1,
  input  [1:0] in_2,
  input  [3:0] in_3,
  input  [3:0] data_src,
  input  [3:0] addr_src,
  input  [2:0] addr_dst,
  input  enable,
  input  [3:0] data_dst
);

  wire and_1_out, clock_1_out, decoder_1_out0, decoder_1_out1, decoder_1_out2, decoder_1_out3,
       decoder_1_out4, decoder_1_out6, decoder_1_out7, decoder_1_out8, decoder_2_out0, decoder_2_out1,
       decoder_2_out2, decoder_2_out3, decoder_2_out4, decoder_2_out6, decoder_2_out7, decoder_3_out4,
       decoder_3_out5, decoder_4_out0, decoder_4_out1, decoder_4_out2, decoder_4_out3, decoder_4_out5,
       decoder_4_out6, decoder_4_out8, not_1_out, not_2_out;
  wire [15:0] A_q, adder_1_out, alu_1_result, B_q, bit_extender_1_out, controlled_buffer_1_out,
       controlled_buffer_2_out, controlled_buffer_3_out, controlled_buffer_5_out, controlled_buffer_7_out,
       controlled_buffer_9_out, controlled_buffer_11_out, controlled_buffer_15_out, controlled_buffer_19_out,
       controlled_buffer_22_out, controlled_buffer_25_out, D_q, IR_q, multiplexer_1_out, multiplexer_2_out,
       PC_q, X_q, Y_q;

  Decoder #(.select(4)) decoder_1 (
    .out0(decoder_1_out0), .out1(decoder_1_out1), .out2(decoder_1_out2), .out3(decoder_1_out3),
    .out4(decoder_1_out4), .out6(decoder_1_out6), .out7(decoder_1_out7), .out8(decoder_1_out8), .sel(data_src));  // open: out5, out9, out10, out11, out12, out13, out14, out15
  Clock clock_1 (.out(clock_1_out));
  Register #(.width(16)) D (.D(controlled_buffer_1_out), .en(decoder_2_out6), .Q(D_q), .clk(and_1_out));  // open: clr
  Multiplexer #(.select(2), .width(16)) multiplexer_1 (
    .in0(A_q), .in1(B_q), .in2(X_q), .in3(Y_q), .out(multiplexer_1_out), .sel(in_1));
  and and_1 (and_1_out, clock_1_out, enable);
  Register #(.width(16)) IR (.D(controlled_buffer_3_out), .en(decoder_2_out7), .Q(IR_q), .clk(and_1_out));  // open: clr
  assign controlled_buffer_1_out = decoder_2_out6 ? controlled_buffer_2_out : 16'bz;  // Controlled_Buffer controlled_buffer_1
  assign controlled_buffer_2_out = decoder_1_out6 ? D_q : 16'bz;  // Controlled_Buffer controlled_buffer_2
  assign controlled_buffer_3_out = decoder_2_out7 ? controlled_buffer_2_out : 16'bz;  // Controlled_Buffer controlled_buffer_3
  assign controlled_buffer_2_out = decoder_1_out7 ? IR_q : 16'bz;  // Controlled_Buffer controlled_buffer_4
  Multiplexer #(.select(2), .width(16)) multiplexer_2 (
    .in0(A_q), .in1(B_q), .in2(X_q), .in3(Y_q), .out(multiplexer_2_out), .sel(in_2));
  Register #(.width(16)) Y (.D(controlled_buffer_5_out), .en(decoder_2_out3), .Q(Y_q), .clk(and_1_out));  // open: clr
  Register #(.width(16)) X (.D(controlled_buffer_7_out), .en(decoder_2_out2), .Q(X_q), .clk(and_1_out));  // open: clr
  Register #(.width(16)) B (.D(controlled_buffer_9_out), .en(decoder_2_out1), .Q(B_q), .clk(and_1_out));  // open: clr
  Register #(.width(16)) A (.D(controlled_buffer_11_out), .en(decoder_2_out0), .Q(A_q), .clk(and_1_out));  // open: clr
  Decoder #(.select(4)) decoder_2 (
    .out0(decoder_2_out0), .out1(decoder_2_out1), .out2(decoder_2_out2), .out3(decoder_2_out3),
    .out4(decoder_2_out4), .out6(decoder_2_out6), .out7(decoder_2_out7), .sel(data_dst));  // open: out5, out8, out9, out10, out11, out12, out13, out14, out15
  assign controlled_buffer_5_out = decoder_2_out3 ? controlled_buffer_2_out : 16'bz;  // Controlled_Buffer controlled_buffer_5
  assign controlled_buffer_2_out = decoder_1_out3 ? Y_q : 16'bz;  // Controlled_Buffer controlled_buffer_6
  assign controlled_buffer_7_out = decoder_2_out2 ? controlled_buffer_2_out : 16'bz;  // Controlled_Buffer controlled_buffer_7
  assign controlled_buffer_2_out = decoder_1_out2 ? X_q : 16'bz;  // Controlled_Buffer controlled_buffer_8
  assign controlled_buffer_9_out = decoder_2_out1 ? controlled_buffer_2_out : 16'bz;  // Controlled_Buffer controlled_buffer_9
  assign controlled_buffer_2_out = decoder_1_out1 ? B_q : 16'bz;  // Controlled_Buffer controlled_buffer_10
  assign controlled_buffer_11_out = decoder_2_out0 ? controlled_buffer_2_out : 16'bz;  // Controlled_Buffer controlled_buffer_11
  assign controlled_buffer_2_out = decoder_1_out0 ? A_q : 16'bz;  // Controlled_Buffer controlled_buffer_12
  // Probe on controlled_buffer_2_out
  assign controlled_buffer_2_out = decoder_1_out8 ? alu_1_result : 16'bz;  // Controlled_Buffer controlled_buffer_13
  assign controlled_buffer_2_out = decoder_1_out4 ? controlled_buffer_19_out : 16'bz;  // Controlled_Buffer controlled_buffer_14
  not not_1 (not_1_out, decoder_2_out4);
  assign controlled_buffer_15_out = decoder_4_out3 ? Y_q : 16'bz;  // Controlled_Buffer controlled_buffer_15
  assign controlled_buffer_15_out = decoder_4_out2 ? X_q : 16'bz;  // Controlled_Buffer controlled_buffer_16
  assign controlled_buffer_15_out = decoder_4_out1 ? B_q : 16'bz;  // Controlled_Buffer controlled_buffer_17
  assign controlled_buffer_15_out = decoder_4_out0 ? A_q : 16'bz;  // Controlled_Buffer controlled_buffer_18
  assign controlled_buffer_19_out = decoder_2_out4 ? controlled_buffer_2_out : 16'bz;  // Controlled_Buffer controlled_buffer_19
  assign controlled_buffer_15_out = decoder_4_out6 ? D_q : 16'bz;  // Controlled_Buffer controlled_buffer_20
  // Probe on controlled_buffer_15_out
  assign controlled_buffer_15_out = decoder_4_out8 ? alu_1_result : 16'bz;  // Controlled_Buffer controlled_buffer_21
  assign controlled_buffer_22_out = decoder_3_out5 ? controlled_buffer_15_out : 16'bz;  // Controlled_Buffer controlled_buffer_22
  assign bit_extender_1_out = {{15{1'b0}}, 1'b1};  // Bit_Extender bit_extender_1
  assign controlled_buffer_22_out = not_2_out ? adder_1_out : 16'bz;  // Controlled_Buffer controlled_buffer_23
  assign controlled_buffer_15_out = decoder_4_out5 ? PC_q : 16'bz;  // Controlled_Buffer controlled_buffer_24
  not not_2 (not_2_out, decoder_3_out5);
  assign controlled_buffer_25_out = decoder_3_out4 ? controlled_buffer_15_out : 16'bz;  // Controlled_Buffer controlled_buffer_25
  Adder #(.width(16)) adder_1 (.a(PC_q), .b(bit_extender_1_out), .out(adder_1_out));  // open: cin, cout
  Register #(.width(16)) PC (.D(controlled_buffer_22_out), .Q(PC_q), .clk(and_1_out));  // open: en, clr
  Decoder #(.select(3)) decoder_3 (
    .out4(decoder_3_out4), .out5(decoder_3_out5), .sel(addr_dst));  // open: out0, out1, out2, out3, out6, out7
  Decoder #(.select(4)) decoder_4 (
    .out0(decoder_4_out0), .out1(decoder_4_out1), .out2(decoder_4_out2), .out3(decoder_4_out3),
    .out5(decoder_4_out5), .out6(decoder_4_out6), .out8(decoder_4_out8), .sel(addr_src));  // open: out4, out7, out9, out10, out11, out12, out13, out14, out15
  // Probe on adder_1_out
  RAM #(.addrWidth(16), .dataWidth(16)) ram_1 (
    .addr(controlled_buffer_25_out), .data(controlled_buffer_19_out), .clk(and_1_out), .ld(not_1_out));  // open: sel, clr
  // Probe on multiplexer_1_out
  // Probe on multiplexer_2_out
  // Probe on controlled_buffer_19_out
  alu alu_1 (
    .result(alu_1_result), .A(multiplexer_1_out), .B(multiplexer_2_out), .op(in_3));  // open: V, N, C_out, Z, C_in
  // Probe on alu_1_result
endmodule

module reg3 (
  input  [3:0] data_src,
  input  clock,
  input  enable,
  input  [3:0] data_dst,
  input  [15:0] data_in,
  output [15:0] data_out
);

  wire and_1_out, decoder_1_out0, decoder_1_out1, decoder_1_out2, decoder_1_out3, decoder_1_out6,
       decoder_1_out7, decoder_1_out15, decoder_2_out0, decoder_2_out1, decoder_2_out2, decoder_2_out3,
       decoder_2_out6, decoder_2_out7, decoder_2_out15;
  wire [15:0] A_q, B_q, controlled_buffer_1_out, controlled_buffer_2_out, controlled_buffer_3_out,
       controlled_buffer_5_out, controlled_buffer_7_out, controlled_buffer_9_out, controlled_buffer_11_out,
       D_q, IR_q, X_q, Y_q;

  Decoder #(.select(4)) decoder_1 (
    .out0(decoder_1_out0), .out1(decoder_1_out1), .out2(decoder_1_out2), .out3(decoder_1_out3),
    .out6(decoder_1_out6), .out7(decoder_1_out7), .out15(decoder_1_out15), .sel(data_src));  // open: out4, out5, out8, out9, out10, out11, out12, out13, out14
  Register #(.width(16)) D (.D(controlled_buffer_1_out), .en(decoder_2_out6), .Q(D_q), .clk(and_1_out));  // open: clr
  and and_1 (and_1_out, clock, enable);
  Register #(.width(16)) IR (.D(controlled_buffer_3_out), .en(decoder_2_out7), .Q(IR_q), .clk(and_1_out));  // open: clr
  assign controlled_buffer_1_out = decoder_2_out6 ? controlled_buffer_2_out : 16'bz;  // Controlled_Buffer controlled_buffer_1
  assign controlled_buffer_2_out = decoder_1_out6 ? D_q : 16'bz;  // Controlled_Buffer controlled_buffer_2
  assign controlled_buffer_3_out = decoder_2_out7 ? controlled_buffer_2_out : 16'bz;  // Controlled_Buffer controlled_buffer_3
  assign controlled_buffer_2_out = decoder_1_out7 ? IR_q : 16'bz;  // Controlled_Buffer controlled_buffer_4
  Register #(.width(16)) Y (.D(controlled_buffer_5_out), .en(decoder_2_out3), .Q(Y_q), .clk(and_1_out));  // open: clr
  Register #(.width(16)) X (.D(controlled_buffer_7_out), .en(decoder_2_out2), .Q(X_q), .clk(and_1_out));  // open: clr
  Register #(.width(16)) B (.D(controlled_buffer_9_out), .en(decoder_2_out1), .Q(B_q), .clk(and_1_out));  // open: clr
  Register #(.width(16)) A (.D(controlled_buffer_11_out), .en(decoder_2_out0), .Q(A_q), .clk(and_1_out));  // open: clr
  Decoder #(.select(4)) decoder_2 (
    .out0(decoder_2_out0), .out1(decoder_2_out1), .out2(decoder_2_out2), .out3(decoder_2_out3),
    .out6(decoder_2_out6), .out7(decoder_2_out7), .out15(decoder_2_out15), .sel(data_dst));  // open: out4, out5, out8, out9, out10, out11, out12, out13, out14
  assign controlled_buffer_5_out = decoder_2_out3 ? controlled_buffer_2_out : 16'bz;  // Controlled_Buffer controlled_buffer_5
  assign controlled_buffer_2_out = decoder_1_out3 ? Y_q : 16'bz;  // Controlled_Buffer controlled_buffer_6
  assign controlled_buffer_7_out = decoder_2_out2 ? controlled_buffer_2_out : 16'bz;  // Controlled_Buffer controlled_buffer_7
  assign controlled_buffer_2_out = decoder_1_out2 ? X_q : 16'bz;  // Controlled_Buffer controlled_buffer_8
  assign controlled_buffer_9_out = decoder_2_out1 ? controlled_buffer_2_out : 16'bz;  // Controlled_Buffer controlled_buffer_9
  assign controlled_buffer_2_out = decoder_1_out1 ? B_q : 16'bz;  // Controlled_Buffer controlled_buffer_10
  assign controlled_buffer_11_out = decoder_2_out0 ? controlled_buffer_2_out : 16'bz;  // Controlled_Buffer controlled_buffer_11
  assign controlled_buffer_2_out = decoder_1_out0 ? A_q : 16'bz;  // Controlled_Buffer controlled_buffer_12
  // Probe on controlled_buffer_2_out
  assign controlled_buffer_2_out = decoder_1_out15 ? data_in : 16'bz;  // Controlled_Buffer controlled_buffer_13
  assign data_out = decoder_2_out15 ? controlled_buffer_2_out : 16'bz;  // Controlled_Buffer controlled_buffer_14
endmodule

module fsm (
  input  [15:0] ir
);

  wire clock_1_out;
  wire [7:0] STATE_q;

  // Probe on ir[15:13]
  // Probe on ir[12:11]
  // Probe on ir[10:9]
  // Probe on ir[4:0]
  // Probe on ir[8:5]
  Clock clock_1 (.out(clock_1_out));
  Register STATE (.Q(STATE_q), .clk(clock_1_out));  // open: D, en, clr
endmodule

module reg4 (
  input  [3:0] in_1,
  input  [3:0] in_2,
  input  in_3,
  input  [3:0] in_4,
  input  [3:0] data_dest,
  input  [3:0] addr_dest,
  input  [3:0] data_src,
  input  [15:0] data_in,
  input  [3:0] addr_src,
  output [15:0] data_out
);

  wire and_1_out, clock_1_out, decoder_1_out0, decoder_1_out1, decoder_1_out2, decoder_1_out3,
       decoder_1_out4, decoder_1_out5, decoder_1_out6, decoder_1_out15, decoder_2_out0, decoder_2_out1,
       decoder_2_out2, decoder_2_out3, decoder_2_out4, decoder_2_out5, decoder_2_out6, decoder_2_out7,
       decoder_2_out15, decoder_4_out0, decoder_4_out1, decoder_4_out2, decoder_4_out3, decoder_4_out4,
       decoder_4_out5, decoder_4_out6, decoder_4_out7, decoder_4_out15;
  wire [15:0] A_q, alu_1_result, B_q, controlled_buffer_1_out, controlled_buffer_2_out,
       controlled_buffer_3_out, controlled_buffer_4_out, controlled_buffer_5_out, controlled_buffer_6_out,
       controlled_buffer_7_out, controlled_buffer_8_out, controlled_buffer_18_out, D_q, IR_q,
       multiplexer_1_out, multiplexer_2_out, PC_q, X_q, Y_q;

  Clock clock_1 (.out(clock_1_out));
  and and_1 (and_1_out, in_3, clock_1_out);
  Decoder #(.select(4)) decoder_1 (
    .out0(decoder_1_out0), .out1(decoder_1_out1), .out2(decoder_1_out2), .out3(decoder_1_out3),
    .out4(decoder_1_out4), .out5(decoder_1_out5), .out6(decoder_1_out6), .out15(decoder_1_out15),
    .sel(data_dest));  // open: out7, out8, out9, out10, out11, out12, out13, out14
  Decoder #(.select(4)) decoder_2 (
    .out0(decoder_2_out0), .out1(decoder_2_out1), .out2(decoder_2_out2), .out3(decoder_2_out3),
    .out4(decoder_2_out4), .out5(decoder_2_out5), .out6(decoder_2_out6), .out7(decoder_2_out7),
    .out15(decoder_2_out15), .sel(data_src));  // open: out8, out9, out10, out11, out12, out13, out14
  Register #(.width(16)) A (.D(controlled_buffer_1_out), .en(decoder_1_out0), .Q(A_q), .clk(and_1_out));  // open: clr
  Register #(.width(16)) B (.D(controlled_buffer_2_out), .en(decoder_1_out1), .Q(B_q), .clk(and_1_out));  // open: clr
  Register #(.width(16)) X (.D(controlled_buffer_3_out), .en(decoder_1_out2), .Q(X_q), .clk(and_1_out));  // open: clr
  Register #(.width(16)) Y (.D(controlled_buffer_4_out), .en(decoder_1_out3), .Q(Y_q), .clk(and_1_out));  // open: clr
  Register #(.width(16)) D (.D(controlled_buffer_5_out), .en(decoder_1_out4), .Q(D_q), .clk(and_1_out));  // open: clr
  Register #(.width(16)) IR (.D(controlled_buffer_7_out), .en(decoder_1_out5), .Q(IR_q), .clk(and_1_out));  // open: clr
  Register #(.width(16)) PC (.D(controlled_buffer_8_out), .en(decoder_1_out6), .Q(PC_q), .clk(and_1_out));  // open: clr
  Multiplexer #(.select(4), .width(16)) multiplexer_1 (
    .in0(A_q), .in1(B_q), .in2(X_q), .in3(Y_q), .in4(D_q), .in5(IR_q), .in6(PC_q), .out(multiplexer_1_out),
    .sel(in_1));  // open: in7, in8, in9, in10, in11, in12, in13, in14, in15
  assign controlled_buffer_1_out = decoder_1_out0 ? controlled_buffer_6_out : 16'bz;  // Controlled_Buffer controlled_buffer_1
  assign controlled_buffer_2_out = decoder_1_out1 ? controlled_buffer_6_out : 16'bz;  // Controlled_Buffer controlled_buffer_2
  assign controlled_buffer_3_out = decoder_1_out2 ? controlled_buffer_6_out : 16'bz;  // Controlled_Buffer controlled_buffer_3
  assign controlled_buffer_4_out = decoder_1_out3 ? controlled_buffer_6_out : 16'bz;  // Controlled_Buffer controlled_buffer_4
  assign controlled_buffer_5_out = decoder_1_out4 ? controlled_buffer_6_out : 16'bz;  // Controlled_Buffer controlled_buffer_5
  assign controlled_buffer_6_out = decoder_2_out15 ? data_in : 16'bz;  // Controlled_Buffer controlled_buffer_6
  assign controlled_buffer_7_out = decoder_1_out5 ? controlled_buffer_6_out : 16'bz;  // Controlled_Buffer controlled_buffer_7
  assign controlled_buffer_8_out = decoder_1_out6 ? controlled_buffer_6_out : 16'bz;  // Controlled_Buffer controlled_buffer_8
  Multiplexer #(.select(4), .width(16)) multiplexer_2 (
    .in0(A_q), .in1(B_q), .in2(X_q), .in3(Y_q), .in4(D_q), .in5(IR_q), .in6(PC_q), .in13({16{1'b0}}),
    .in14(16'h1), .in15({16{1'b1}}), .out(multiplexer_2_out), .sel(in_4));  // open: in7, in8, in9, in10, in11, in12
  alu alu_1 (
    .result(alu_1_result), .A(multiplexer_1_out), .B(multiplexer_2_out), .op(in_2));  // open: V, N, C_out, Z, C_in
  assign controlled_buffer_6_out = decoder_2_out0 ? A_q : 16'bz;  // Controlled_Buffer controlled_buffer_9
  assign controlled_buffer_6_out = decoder_2_out1 ? B_q : 16'bz;  // Controlled_Buffer controlled_buffer_10
  assign controlled_buffer_6_out = decoder_2_out2 ? X_q : 16'bz;  // Controlled_Buffer controlled_buffer_11
  assign controlled_buffer_6_out = decoder_2_out3 ? Y_q : 16'bz;  // Controlled_Buffer controlled_buffer_12
  assign controlled_buffer_6_out = decoder_2_out4 ? D_q : 16'bz;  // Controlled_Buffer controlled_buffer_13
  assign controlled_buffer_6_out = decoder_2_out5 ? IR_q : 16'bz;  // Controlled_Buffer controlled_buffer_14
  assign controlled_buffer_6_out = decoder_2_out6 ? PC_q : 16'bz;  // Controlled_Buffer controlled_buffer_15
  assign controlled_buffer_6_out = decoder_2_out7 ? alu_1_result : 16'bz;  // Controlled_Buffer controlled_buffer_16
  assign data_out = decoder_1_out15 ? controlled_buffer_6_out : 16'bz;  // Controlled_Buffer controlled_buffer_17
  // Probe on controlled_buffer_6_out
  assign controlled_buffer_18_out = decoder_4_out7 ? alu_1_result : 16'bz;  // Controlled_Buffer controlled_buffer_18
  assign controlled_buffer_18_out = decoder_4_out0 ? A_q : 16'bz;  // Controlled_Buffer controlled_buffer_19
  assign controlled_buffer_18_out = decoder_4_out1 ? B_q : 16'bz;  // Controlled_Buffer controlled_buffer_20
  assign controlled_buffer_18_out = decoder_4_out2 ? X_q : 16'bz;  // Controlled_Buffer controlled_buffer_21
  assign controlled_buffer_18_out = decoder_4_out3 ? Y_q : 16'bz;  // Controlled_Buffer controlled_buffer_22
  // Probe on controlled_buffer_18_out
  assign controlled_buffer_18_out = decoder_4_out4 ? D_q : 16'bz;  // Controlled_Buffer controlled_buffer_23
  assign controlled_buffer_18_out = decoder_4_out5 ? IR_q : 16'bz;  // Controlled_Buffer controlled_buffer_24
  assign controlled_buffer_18_out = decoder_4_out6 ? PC_q : 16'bz;  // Controlled_Buffer controlled_buffer_25
  assign controlled_buffer_18_out = decoder_4_out15 ? controlled_buffer_6_out : 16'bz;  // Controlled_Buffer controlled_buffer_26
  RAM #(.addrWidth(16), .dataWidth(16)) ram_1 (.addr(controlled_buffer_18_out));  // open: data, sel, clk, ld, clr
  Decoder #(.select(4)) decoder_3 (.sel(addr_dest));  // open: out0, out1, out2, out3, out4, out5, out6, out7, out8, out9, out10, out11, out12, out13, out14, out15
  Decoder #(.select(4)) decoder_4 (
    .out0(decoder_4_out0), .out1(decoder_4_out1), .out2(decoder_4_out2), .out3(decoder_4_out3),
    .out4(decoder_4_out4), .out5(decoder_4_out5), .out6(decoder_4_out6), .out7(decoder_4_out7),
    .out15(decoder_4_out15), .sel(addr_src));  // open: out8, out9, out10, out11, out12, out13, out14

  // Notes on the sheet:
  //   DATA BUS
  //   ADDRESS BUS
endmodule
