// Logisim project clock1.circ as structural Verilog: 3 circuits, main circuit main
module main (
  input  [3:0] in_1
);

  wire and_1_out, clock_1_out, controlled_buffer_1_out, down2_1_end, down_1_c, not_1_out, xnor_1_out;
  wire [3:0] down2_1_out, down_1_out;

  Clock clock_1 (.out(clock_1_out));
  assign controlled_buffer_1_out = xnor_1_out ? clock_1_out : 1'bz;  // Controlled_Buffer controlled_buffer_1
  xnor xnor_1 (xnor_1_out, down_1_c, not_1_out);
  Pull_Resistor pull_resistor_1 (.node(controlled_buffer_1_out));
  not not_1 (not_1_out, down2_1_end);
  down down_1 (.en(and_1_out), .out(down_1_out), .c(down_1_c));
  and and_1 (and_1_out, clock_1_out, ~down2_1_end);  // AND_Gate
  down2 down2_1 (.in(in_1), .clk(controlled_buffer_1_out), .en(1'b1), .\end (down2_1_end), .out(down2_1_out));
  LED led_1 (.in(down_1_c));
  DotMatrix #(.matrixcols(1), .matrixrows(4)) dotmatrix_1 (.col0(down_1_out));
  DotMatrix #(.matrixcols(1), .matrixrows(4)) dotmatrix_2 (.col0(down2_1_out));
endmodule

module down (
  input  en,
  output [3:0] out,
  output c
);

  wire [3:0] bit_extender_1_out;

  assign bit_extender_1_out = {{3{1'b1}}, 1'b1};  // Bit_Extender bit_extender_1
  Counter #(.width(4), .max('hf)) counter_1 (
    .load(1'b1), .D(bit_extender_1_out), .Q(out), .carry(c), .clk(en));  // open: count, clr
endmodule

module down2 (
  input  [3:0] in,
  input  clk,
  input  en,
  output \end ,
  output [3:0] out
);

  wire and_1_out, and_2_out, j_k_ff_1_qn, not_1_out;

  and and_1 (and_1_out, clk, en);
  Counter #(.width(4), .max('hf)) counter_1 (
    .load(1'b1), .D(in), .count(j_k_ff_1_qn), .Q(out), .clk(and_1_out));  // open: carry, clr
  and and_2 (and_2_out, out[0], ~out[1], ~out[2], ~out[3]);  // AND_Gate
  J_K_Flip_Flop j_k_ff_1 (
    .J(and_2_out), .clk(and_1_out), .K(not_1_out), .Q(\end ), .Qn(j_k_ff_1_qn));  // open: preset, en, reset
  not not_1 (not_1_out, and_2_out);
endmodule
