// Logisim project fetch.circ as structural Verilog: 1 circuit, main circuit main
module main (
  input  pc_wrt,
  input  ir_bus,
  input  ram_wrt,
  input  ir_wrt
);

  wire clock_1_out, not_1_out, rst_out;
  wire [15:0] adder_1_out, bit_extender_1_out, pc_q, ram_2_data, register_1_q;

  Clock clock_1 (.out(clock_1_out));
  RAM #(.addrWidth(2), .dataWidth(32)) ram_1 ();  // open: addr, data, sel, clk, ld, clr
  Register #(.width(16)) pc (.D(adder_1_out), .en(pc_wrt), .Q(pc_q), .clk(clock_1_out), .clr(rst_out));
  Button rst (.out(rst_out));
  assign bit_extender_1_out = {{15{1'b0}}, 1'b1};  // Bit_Extender bit_extender_1
  not not_1 (not_1_out, ram_wrt);
  Adder #(.width(16)) adder_1 (.a(pc_q), .b(bit_extender_1_out), .out(adder_1_out));  // open: cin, cout
  RAM #(.addrWidth(16), .dataWidth(16)) ram_2 (
    .addr(pc_q), .data(ram_2_data), .clk(clock_1_out), .ld(not_1_out));  // open: sel, clr
  assign ram_2_data = ir_bus ? register_1_q : 16'bz;  // Controlled_Buffer controlled_buffer_1
  // Probe on ram_2_data
  // Probe on adder_1_out
  // Probe on register_1_q
  Register #(.width(16)) register_1 (.D(ram_2_data), .en(ir_wrt), .Q(register_1_q), .clk(clock_1_out));  // open: clr
endmodule
