// Logisim project flasher.circ as structural Verilog: 1 circuit, main circuit main
module main (
);

  wire clock_1_out;
  wire [3:0] counter_1_q, rom_1_data;

  Clock clock_1 (.out(clock_1_out));
  Counter #(.width(4), .max('hf)) counter_1 (.Q(counter_1_q), .clk(clock_1_out));  // open: load, D, count, carry, clr
  ROM #(.addrWidth(4), .dataWidth(4)) rom_1 (.addr(counter_1_q), .data(rom_1_data), .sel(1'b1));
  LED led_1 (.in(rom_1_data[0]));
  LED led_2 (.in(rom_1_data[1]));
  LED led_3 (.in(rom_1_data[2]));
  LED led_4 (.in(rom_1_data[3]));

  // Notes on the sheet:
  //   contents of rom_1 (hex, n*v repeats v):
  //   1 2 4 8 4 2 1 8 c e f 7 3 1
endmodule
