// Logisim project rand.circ as structural Verilog: 1 circuit, main circuit main
module main (
  input  [7:0] in_1,
  input  [7:0] in_2
);

  wire adder_1_cout, clock_1_out;
  wire [3:0] bit_extender_1_out, bit_extender_2_out, bit_extender_2_out_2;
  wire [4:0] bitadder_1_out;
  wire [6:0] random_2_out;
  wire [15:0] random_1_out;

  Clock clock_1 (.out(clock_1_out));
  Random #(.width(16)) random_1 (.clk(clock_1_out), .out(random_1_out));  // open: next, clr
  Adder adder_1 (.a(in_1), .b(in_2), .cout(adder_1_cout));  // open: out, cin
  BitAdder #(.width(16)) bitadder_1 (.in0(random_1_out), .out(bitadder_1_out));
  // Probe on bitadder_1_out
  Hex_Digit_Display hex_digit_display_1 (.value(bit_extender_1_out));  // open: dp
  assign bit_extender_1_out = {{3{1'b0}}, adder_1_cout};  // Bit_Extender bit_extender_1
  Random #(.width(7)) random_2 (.clk(clock_1_out), .out(random_2_out));  // open: next, clr
  Hex_Digit_Display hex_digit_display_2 (.value(bit_extender_2_out_2));  // open: dp
  Hex_Digit_Display hex_digit_display_3 (.value(bit_extender_2_out));  // open: dp
  assign {bit_extender_2_out_2, bit_extender_2_out} = {{3{1'b0}}, bitadder_1_out};  // Bit_Extender bit_extender_2
  TTY tty_1 (.data(random_2_out), .clk(clock_1_out));  // open: we, clr
  DotMatrix #(.matrixcols(8), .matrixrows(8)) dotmatrix_1 (.col0({bit_extender_2_out_2, bit_extender_2_out}));  // open: col1, col2, col3, col4, col5, col6, col7
endmodule
