// Logisim project bounce.circ as structural Verilog: 3 circuits, main circuit main
module main (
);

  wire clock_1_out;
  wire [4:0] ball_1_x, ball_2_x;
  wire [31:0] decoder_1_out31, demultiplexer_1_out0, demultiplexer_1_out1, demultiplexer_1_out2,
       demultiplexer_1_out3, demultiplexer_1_out4, demultiplexer_1_out5, demultiplexer_1_out6,
       demultiplexer_1_out7, demultiplexer_1_out8, demultiplexer_1_out9, demultiplexer_1_out10,
       demultiplexer_1_out11, demultiplexer_1_out12, demultiplexer_1_out13, demultiplexer_1_out14,
       demultiplexer_1_out15, demultiplexer_1_out16, demultiplexer_1_out17, demultiplexer_1_out18,
       demultiplexer_1_out19, demultiplexer_1_out20, demultiplexer_1_out21, demultiplexer_1_out22,
       demultiplexer_1_out23, demultiplexer_1_out24, demultiplexer_1_out25, demultiplexer_1_out26,
       demultiplexer_1_out27, demultiplexer_1_out28, demultiplexer_1_out29, demultiplexer_1_out30,
       demultiplexer_1_out31;

  Clock clock_1 (.out(clock_1_out));
  ball ball_1 (.clk(clock_1_out), .x(ball_1_x));
  ball ball_2 (.clk(clock_1_out), .x(ball_2_x));
  // Probe on ball_2_x
  // Probe on ball_1_x
  // Probe on ball_1_x
  DotMatrix #(.matrixcols(32), .matrixrows(32)) dotmatrix_1 (
    .col0(demultiplexer_1_out0), .col1(demultiplexer_1_out1), .col2(demultiplexer_1_out2),
    .col3(demultiplexer_1_out3), .col4(demultiplexer_1_out4), .col5(demultiplexer_1_out5),
    .col6(demultiplexer_1_out6), .col7(demultiplexer_1_out7), .col8(demultiplexer_1_out8),
    .col9(demultiplexer_1_out9), .col10(demultiplexer_1_out10), .col11(demultiplexer_1_out11),
    .col12(demultiplexer_1_out12), .col13(demultiplexer_1_out13), .col14(demultiplexer_1_out14),
    .col15(demultiplexer_1_out15), .col16(demultiplexer_1_out16), .col17(demultiplexer_1_out17),
    .col18(demultiplexer_1_out18), .col19(demultiplexer_1_out19), .col20(demultiplexer_1_out20),
    .col21(demultiplexer_1_out21), .col22(demultiplexer_1_out22), .col23(demultiplexer_1_out23),
    .col24(demultiplexer_1_out24), .col25(demultiplexer_1_out25), .col26(demultiplexer_1_out26),
    .col27(demultiplexer_1_out27), .col28(demultiplexer_1_out28), .col29(demultiplexer_1_out29),
    .col30(demultiplexer_1_out30), .col31(demultiplexer_1_out31));
  Decoder #(.select(5)) decoder_1 (
    .out0(decoder_1_out31[31]), .out1(decoder_1_out31[30]), .out2(decoder_1_out31[29]),
    .out3(decoder_1_out31[28]), .out4(decoder_1_out31[27]), .out5(decoder_1_out31[26]),
    .out6(decoder_1_out31[25]), .out7(decoder_1_out31[24]), .out8(decoder_1_out31[23]),
    .out9(decoder_1_out31[22]), .out10(decoder_1_out31[21]), .out11(decoder_1_out31[20]),
    .out12(decoder_1_out31[19]), .out13(decoder_1_out31[18]), .out14(decoder_1_out31[17]),
    .out15(decoder_1_out31[16]), .out16(decoder_1_out31[15]), .out17(decoder_1_out31[14]),
    .out18(decoder_1_out31[13]), .out19(decoder_1_out31[12]), .out20(decoder_1_out31[11]),
    .out21(decoder_1_out31[10]), .out22(decoder_1_out31[9]), .out23(decoder_1_out31[8]),
    .out24(decoder_1_out31[7]), .out25(decoder_1_out31[6]), .out26(decoder_1_out31[5]),
    .out27(decoder_1_out31[4]), .out28(decoder_1_out31[3]), .out29(decoder_1_out31[2]),
    .out30(decoder_1_out31[1]), .out31(decoder_1_out31[0]), .sel(ball_1_x));
  Demultiplexer #(.select(5), .width(32)) demultiplexer_1 (
    .out0(demultiplexer_1_out0), .out1(demultiplexer_1_out1), .out2(demultiplexer_1_out2),
    .out3(demultiplexer_1_out3), .out4(demultiplexer_1_out4), .out5(demultiplexer_1_out5),
    .out6(demultiplexer_1_out6), .out7(demultiplexer_1_out7), .out8(demultiplexer_1_out8),
    .out9(demultiplexer_1_out9), .out10(demultiplexer_1_out10), .out11(demultiplexer_1_out11),
    .out12(demultiplexer_1_out12), .out13(demultiplexer_1_out13), .out14(demultiplexer_1_out14),
    .out15(demultiplexer_1_out15), .out16(demultiplexer_1_out16), .out17(demultiplexer_1_out17),
    .out18(demultiplexer_1_out18), .out19(demultiplexer_1_out19), .out20(demultiplexer_1_out20),
    .out21(demultiplexer_1_out21), .out22(demultiplexer_1_out22), .out23(demultiplexer_1_out23),
    .out24(demultiplexer_1_out24), .out25(demultiplexer_1_out25), .out26(demultiplexer_1_out26),
    .out27(demultiplexer_1_out27), .out28(demultiplexer_1_out28), .out29(demultiplexer_1_out29),
    .out30(demultiplexer_1_out30), .out31(demultiplexer_1_out31), .in(decoder_1_out31), .sel(ball_2_x));
endmodule

module ball (
  input  clk,
  output [4:0] x
);

  wire adder_1_cout;
  wire [4:0] DX_q, negator_1_out, X_q;

  Register #(.width(5)) u_X (.D(x), .Q(X_q), .clk(clk));  // open: en, clr
  Negator #(.width(5)) negator_1 (.in(DX_q), .out(negator_1_out));
  Register #(.width(5)) DX (.D(negator_1_out), .Q(DX_q), .clk(adder_1_cout));  // open: en, clr
  Adder #(.width(5)) adder_1 (.a(DX_q), .b(X_q), .out(x), .cout(adder_1_cout));  // open: cin
endmodule

module q (
);

  wire adder_1_cout, adder_2_cout, clock_1_out, counter_1_carry;
  wire [4:0] adder_1_out, adder_2_out, DX_2_q, DX_q, multiplexer_1_out, multiplexer_2_out, negator_1_out,
       negator_2_out, random_1_out, random_2_out, X_2_q, X_q;
  wire [31:0] decoder_1_out31, demultiplexer_1_out0, demultiplexer_1_out1, demultiplexer_1_out2,
       demultiplexer_1_out3, demultiplexer_1_out4, demultiplexer_1_out5, demultiplexer_1_out6,
       demultiplexer_1_out7, demultiplexer_1_out8, demultiplexer_1_out9, demultiplexer_1_out10,
       demultiplexer_1_out11, demultiplexer_1_out12, demultiplexer_1_out13, demultiplexer_1_out14,
       demultiplexer_1_out15, demultiplexer_1_out16, demultiplexer_1_out17, demultiplexer_1_out18,
       demultiplexer_1_out19, demultiplexer_1_out20, demultiplexer_1_out21, demultiplexer_1_out22,
       demultiplexer_1_out23, demultiplexer_1_out24, demultiplexer_1_out25, demultiplexer_1_out26,
       demultiplexer_1_out27, demultiplexer_1_out28, demultiplexer_1_out29, demultiplexer_1_out30,
       demultiplexer_1_out31;

  Random #(.width(5)) random_1 (.clk(counter_1_carry), .out(random_1_out));  // open: next, clr
  Clock clock_1 (.out(clock_1_out));
  Multiplexer #(.width(5)) multiplexer_1 (
    .in0(adder_2_out), .in1(random_2_out), .out(multiplexer_1_out), .sel(counter_1_carry));
  Multiplexer #(.width(5)) multiplexer_2 (
    .in0(adder_1_out), .in1(random_1_out), .out(multiplexer_2_out), .sel(counter_1_carry));
  Counter counter_1 (.carry(counter_1_carry), .clk(clock_1_out));  // open: load, D, count, Q, clr
  Register #(.width(5)) DX (.D(negator_1_out), .Q(DX_q), .clk(adder_1_cout));  // open: en, clr
  Negator #(.width(5)) negator_1 (.in(DX_q), .out(negator_1_out));
  Register #(.width(5)) X (.D(multiplexer_2_out), .Q(X_q), .clk(clock_1_out));  // open: en, clr
  Negator #(.width(5)) negator_2 (.in(DX_2_q), .out(negator_2_out));
  Register #(.width(5)) DX_2 (.D(negator_2_out), .Q(DX_2_q), .clk(adder_2_cout));  // open: en, clr
  Register #(.width(5)) X_2 (.D(multiplexer_1_out), .Q(X_2_q), .clk(clock_1_out));  // open: en, clr
  Random #(.width(5)) random_2 (.clk(counter_1_carry), .out(random_2_out));  // open: next, clr
  LED led_1 (.in(counter_1_carry));
  Adder #(.width(5)) adder_1 (.a(DX_q), .b(X_q), .out(adder_1_out), .cout(adder_1_cout));  // open: cin
  Adder #(.width(5)) adder_2 (.a(DX_2_q), .b(X_2_q), .out(adder_2_out), .cout(adder_2_cout));  // open: cin
  DotMatrix #(.matrixcols(32), .matrixrows(32)) dotmatrix_1 (
    .col0(demultiplexer_1_out0), .col1(demultiplexer_1_out1), .col2(demultiplexer_1_out2),
    .col3(demultiplexer_1_out3), .col4(demultiplexer_1_out4), .col5(demultiplexer_1_out5),
    .col6(demultiplexer_1_out6), .col7(demultiplexer_1_out7), .col8(demultiplexer_1_out8),
    .col9(demultiplexer_1_out9), .col10(demultiplexer_1_out10), .col11(demultiplexer_1_out11),
    .col12(demultiplexer_1_out12), .col13(demultiplexer_1_out13), .col14(demultiplexer_1_out14),
    .col15(demultiplexer_1_out15), .col16(demultiplexer_1_out16), .col17(demultiplexer_1_out17),
    .col18(demultiplexer_1_out18), .col19(demultiplexer_1_out19), .col20(demultiplexer_1_out20),
    .col21(demultiplexer_1_out21), .col22(demultiplexer_1_out22), .col23(demultiplexer_1_out23),
    .col24(demultiplexer_1_out24), .col25(demultiplexer_1_out25), .col26(demultiplexer_1_out26),
    .col27(demultiplexer_1_out27), .col28(demultiplexer_1_out28), .col29(demultiplexer_1_out29),
    .col30(demultiplexer_1_out30), .col31(demultiplexer_1_out31));
  Decoder #(.select(5)) decoder_1 (
    .out0(decoder_1_out31[31]), .out1(decoder_1_out31[30]), .out2(decoder_1_out31[29]),
    .out3(decoder_1_out31[28]), .out4(decoder_1_out31[27]), .out5(decoder_1_out31[26]),
    .out6(decoder_1_out31[25]), .out7(decoder_1_out31[24]), .out8(decoder_1_out31[23]),
    .out9(decoder_1_out31[22]), .out10(decoder_1_out31[21]), .out11(decoder_1_out31[20]),
    .out12(decoder_1_out31[19]), .out13(decoder_1_out31[18]), .out14(decoder_1_out31[17]),
    .out15(decoder_1_out31[16]), .out16(decoder_1_out31[15]), .out17(decoder_1_out31[14]),
    .out18(decoder_1_out31[13]), .out19(decoder_1_out31[12]), .out20(decoder_1_out31[11]),
    .out21(decoder_1_out31[10]), .out22(decoder_1_out31[9]), .out23(decoder_1_out31[8]),
    .out24(decoder_1_out31[7]), .out25(decoder_1_out31[6]), .out26(decoder_1_out31[5]),
    .out27(decoder_1_out31[4]), .out28(decoder_1_out31[3]), .out29(decoder_1_out31[2]),
    .out30(decoder_1_out31[1]), .out31(decoder_1_out31[0]), .sel(adder_1_out));
  Demultiplexer #(.select(5), .width(32)) demultiplexer_1 (
    .out0(demultiplexer_1_out0), .out1(demultiplexer_1_out1), .out2(demultiplexer_1_out2),
    .out3(demultiplexer_1_out3), .out4(demultiplexer_1_out4), .out5(demultiplexer_1_out5),
    .out6(demultiplexer_1_out6), .out7(demultiplexer_1_out7), .out8(demultiplexer_1_out8),
    .out9(demultiplexer_1_out9), .out10(demultiplexer_1_out10), .out11(demultiplexer_1_out11),
    .out12(demultiplexer_1_out12), .out13(demultiplexer_1_out13), .out14(demultiplexer_1_out14),
    .out15(demultiplexer_1_out15), .out16(demultiplexer_1_out16), .out17(demultiplexer_1_out17),
    .out18(demultiplexer_1_out18), .out19(demultiplexer_1_out19), .out20(demultiplexer_1_out20),
    .out21(demultiplexer_1_out21), .out22(demultiplexer_1_out22), .out23(demultiplexer_1_out23),
    .out24(demultiplexer_1_out24), .out25(demultiplexer_1_out25), .out26(demultiplexer_1_out26),
    .out27(demultiplexer_1_out27), .out28(demultiplexer_1_out28), .out29(demultiplexer_1_out29),
    .out30(demultiplexer_1_out30), .out31(demultiplexer_1_out31), .in(decoder_1_out31), .sel(adder_2_out));
endmodule
