// Logisim project cpu.circ as structural Verilog: 1 circuit, main circuit main
module main (
);

  wire clock_1_out;
  wire [3:0] rom_2_data, state_q;
  wire [15:0] adder_1_out, bit_extender_1_out, IR_q, multiplexer_1_out, PC_q, ram_1_data, rom_1_data;

  Clock clock_1 (.out(clock_1_out));
  Register #(.width(16)) PC (.D(adder_1_out), .Q(PC_q), .clk(clock_1_out));  // open: en, clr
  // Probe on rom_1_data[0]
  Multiplexer #(.width(16)) multiplexer_1 (.in0(PC_q), .in1(IR_q), .out(multiplexer_1_out), .sel(rom_1_data[0]));
  Register #(.width(4)) state (.D(rom_2_data), .Q(state_q), .clk(clock_1_out));  // open: en, clr
  assign bit_extender_1_out = {{15{1'b0}}, 1'b1};  // Bit_Extender bit_extender_1
  // Probe on multiplexer_1_out
  // Probe on adder_1_out
  Adder #(.width(16)) adder_1 (.a(PC_q), .b(bit_extender_1_out), .out(adder_1_out));  // open: cin, cout
  RAM #(.addrWidth(16), .dataWidth(16), .bus("separate")) ram_1 (
    .addr(multiplexer_1_out), .data(ram_1_data), .str(rom_1_data[1]), .clk(clock_1_out));  // open: din, sel, ld, clr
  ROM #(.addrWidth(4), .dataWidth(16)) rom_1 (.addr(state_q), .data(rom_1_data));  // open: sel
  // Probe on IR_q
  Register #(.width(16)) IR (.D(ram_1_data), .Q(IR_q), .clk(clock_1_out));  // open: en, clr
  ROM #(.addrWidth(4), .dataWidth(4)) rom_2 (.addr(state_q), .data(rom_2_data));  // open: sel

  // Notes on the sheet:
  //   contents of rom_2 (hex, n*v repeats v):
  //   1 2 4 5 6 7 9 9 0 a 3 4
endmodule
