// Logisim project qwerty.circ as structural Verilog: 1 circuit, main circuit main
module main (
);

  wire clock_1_out;
  wire [3:0] counter_1_q;
  wire [6:0] bit_extender_2_out, ram_1_data, random_1_out;

  Clock clock_1 (.out(clock_1_out));
  LED led_1 (.in(clock_1_out));
  Bit_Extender #(.in_width(1), .out_width(4)) bit_extender_1 (.in(clock_1_out));  // open: out
  Counter #(.width(4), .max('hf)) counter_1 (.Q(counter_1_q), .clk(clock_1_out));  // open: load, D, count, carry, clr
  DotMatrix dotmatrix_1 (
    .col0(random_1_out), .col1(bit_extender_2_out), .col2(bit_extender_2_out), .col3(bit_extender_2_out),
    .col4(ram_1_data));
  Random #(.width(7)) random_1 (.clk(clock_1_out), .out(random_1_out));  // open: next, clr
  RAM #(.addrWidth(4), .dataWidth(7)) ram_1 (
    .addr(counter_1_q), .data(ram_1_data), .clk(clock_1_out), .ld(1'b1));  // open: sel, clr
  Hex_Digit_Display hex_digit_display_1 (.value(counter_1_q));  // open: dp
  assign bit_extender_2_out = {{3{1'b0}}, counter_1_q};  // Bit_Extender bit_extender_2
endmodule
