// Logisim project reg2.circ as structural Verilog: 1 circuit, main circuit main
module main (
  input  [1:0] addr_src,
  input  mem_wrt,
  input  reg_enbl,
  input  [1:0] reg_sel
);

  wire and_1_out, and_2_out, and_3_out, and_4_out, clock_1_out, decoder_1_out0, decoder_1_out1,
       decoder_1_out2, decoder_1_out3;
  wire [1:0] undriven_3;
  wire [15:0] A_q, B_q, C_q, D_q, multiplexer_1_out, multiplexer_2_out, PC_q, ram_1_data, undriven,
       undriven_2, undriven_4, undriven_5;

  Clock clock_1 (.out(clock_1_out));
  Register #(.width(16)) PC (.D(undriven), .Q(PC_q), .clk(clock_1_out));  // open: en, clr
  Multiplexer #(.select(2), .width(16)) multiplexer_1 (
    .in0(PC_q), .out(multiplexer_1_out), .sel(addr_src));  // open: in1, in2, in3
  RAM #(.addrWidth(16), .dataWidth(16)) ram_1 (
    .addr(multiplexer_1_out), .data(ram_1_data), .clk(clock_1_out), .ld(mem_wrt));  // open: sel, clr
  // Probe on ram_1_data
  Decoder #(.select(2)) decoder_1 (
    .out0(decoder_1_out0), .out1(decoder_1_out1), .out2(decoder_1_out2), .out3(decoder_1_out3), .sel(reg_sel));
  Register #(.width(16)) A (.D(undriven_2), .en(reg_enbl), .Q(A_q), .clk(and_1_out));  // open: clr
  and and_1 (and_1_out, clock_1_out, decoder_1_out0);
  Multiplexer #(.select(2), .width(16)) multiplexer_2 (
    .out(multiplexer_2_out), .sel(undriven_3));  // open: in0, in1, in2, in3
  Register #(.width(16)) B (.D(multiplexer_2_out), .en(reg_enbl), .Q(B_q), .clk(and_2_out));  // open: clr
  and and_2 (and_2_out, clock_1_out, decoder_1_out1);
  and and_3 (and_3_out, clock_1_out, decoder_1_out2);
  Register #(.width(16)) C (.D(undriven_4), .en(reg_enbl), .Q(C_q), .clk(and_3_out));  // open: clr
  and and_4 (and_4_out, clock_1_out, decoder_1_out3);
  Register #(.width(16)) D (.D(undriven_5), .en(reg_enbl), .Q(D_q), .clk(and_4_out));  // open: clr
endmodule
