// Logisim project reg3.circ as structural Verilog: 1 circuit, main circuit main
module main (
  input  cnt_out,
  input  r0_out,
  input  r1_out,
  input  r0_enbl,
  input  r1_enbl,
  input  mem_in,
  input  rand_out,
  input  mem_out,
  input  mem_enbl,
  input  mem_load,
  input  addr_lo_enbl,
  input  addr_hi_enbl,
  input  in_13,
  input  pc_rst
);

  wire button_1_out, clk_out;
  wire [3:0] adr_lo_2_q, adr_lo_q, controlled_buffer_1_out, controlled_buffer_5_out, counter_1_q, r0_q, r1_q,
       random_1_out;
  wire [7:0] adder_1_out, bit_extender_1_out, bit_extender_2_out, multiplexer_1_out, register_1_q;
  wire [15:0] rom_1_data;

  Clock clk (.out(clk_out));
  LED led_1 (.in(controlled_buffer_1_out[1]));
  LED led_2 (.in(controlled_buffer_1_out[2]));
  LED led_3 (.in(controlled_buffer_1_out[3]));
  LED led_4 (.in(controlled_buffer_1_out[0]));
  // Probe on adder_1_out
  assign bit_extender_1_out = {{7{1'b0}}, 1'b0};  // Bit_Extender bit_extender_1
  assign bit_extender_2_out = {{7{1'b0}}, 1'b1};  // Bit_Extender bit_extender_2
  Adder adder_1 (.a(bit_extender_2_out), .b(register_1_q), .out(adder_1_out));  // open: cin, cout
  // Probe on controlled_buffer_1_out
  Multiplexer #(.width(8)) multiplexer_1 (
    .in0(adder_1_out), .in1(bit_extender_1_out), .out(multiplexer_1_out), .sel(rom_1_data[0]));
  Hex_Digit_Display hex_digit_display_1 (.value(controlled_buffer_1_out));  // open: dp
  Register #(.width(4)) r0 (.D(controlled_buffer_1_out), .en(r0_enbl), .Q(r0_q), .clk(clk_out));  // open: clr
  Register #(.width(4)) r1 (.D(controlled_buffer_1_out), .en(r1_enbl), .Q(r1_q), .clk(clk_out));  // open: clr
  assign controlled_buffer_1_out = r0_out ? r0_q : 4'bz;  // Controlled_Buffer controlled_buffer_1
  assign controlled_buffer_1_out = r1_out ? r1_q : 4'bz;  // Controlled_Buffer controlled_buffer_2
  Random #(.width(4)) random_1 (.clk(clk_out), .out(random_1_out));  // open: next, clr
  // Probe on register_1_q
  Register register_1 (.D(multiplexer_1_out), .Q(register_1_q), .clk(clk_out));  // open: en, clr
  assign controlled_buffer_1_out = rom_1_data[1] ? random_1_out : 4'bz;  // Controlled_Buffer controlled_buffer_3
  Register #(.width(4)) adr_lo (
    .D(controlled_buffer_1_out), .en(rom_1_data[3]), .Q(adr_lo_q), .clk(clk_out));  // open: clr
  Register #(.width(4)) adr_lo_2 (
    .D(controlled_buffer_1_out), .en(rom_1_data[2]), .Q(adr_lo_2_q), .clk(clk_out));  // open: clr
  ROM #(.dataWidth(16)) rom_1 (.addr(register_1_q), .data(rom_1_data), .sel(in_13));
  Counter #(.width(4), .max('hf)) counter_1 (.Q(counter_1_q), .clk(clk_out));  // open: load, D, count, carry, clr
  // Probe on rom_1_data
  assign controlled_buffer_1_out = cnt_out ? counter_1_q : 4'bz;  // Controlled_Buffer controlled_buffer_4
  assign controlled_buffer_5_out = rom_1_data[4] ? controlled_buffer_1_out : 4'bz;  // Controlled_Buffer controlled_buffer_5
  // Probe on controlled_buffer_5_out
  Button button_1 (.out(button_1_out));
  assign controlled_buffer_1_out = mem_out ? controlled_buffer_5_out : 4'bz;  // Controlled_Buffer controlled_buffer_6
  RAM #(.dataWidth(4)) ram_1 (
    .addr({adr_lo_2_q, adr_lo_q}), .data(controlled_buffer_5_out), .sel(rom_1_data[5]), .clk(clk_out),
    .ld(rom_1_data[6]), .clr(button_1_out));
  DotMatrix #(.matrixcols(1), .matrixrows(4)) dotmatrix_1 (.col0(controlled_buffer_1_out));

  // Notes on the sheet:
  //   contents of rom_1 (hex, n*v repeats v):
  //   6 a 32 1
endmodule
